# Fritzing sketch Arduino_4x4x4_LED_595 (saved by Fritzing 0.9.3b)
circuit board: 10cm x 5cm
breadboards: 1

parts:
  74HC595 = 74HC595 [package="DIP16 [THT]"]
  74HC595_2 = 74HC595 [package="DIP16 [THT]"]
  74HC595_3 = 74HC595 [package="DIP16 [THT]"]
  R2 = Resistor [tolerance=±5% resistance=220 package=THT]
  ULN2003 = ULN2003A [package="DIP16 [THT]"]
  R3 = Resistor [tolerance=±5% resistance=220 package=THT]
  R4 = Resistor [tolerance=±5% resistance=220 package=THT]
  R6 = Resistor [tolerance=±5% resistance=220 package=THT]
  R7 = Resistor [tolerance=±5% resistance=220 package=THT]
  R8 = Resistor [tolerance=±5% resistance=220 package=THT]
  R9 = Resistor [tolerance=±5% resistance=220 package=THT]
  R10 = Resistor [tolerance=±5% resistance=220 package=THT]
  R11 = Resistor [tolerance=±5% resistance=220 package=THT]
  R12 = Resistor [tolerance=±5% resistance=220 package=THT]
  R14 = Resistor [tolerance=±5% resistance=220 package=THT]
  R15 = Resistor [tolerance=±5% resistance=220 package=THT]
  R16 = Resistor [tolerance=±5% resistance=220 package=THT]
  R17 = Resistor [tolerance=±5% resistance=220 package=THT]
  R18 = Resistor [tolerance=±5% resistance=220 package=THT]
  R19 = Resistor [tolerance=±5% resistance=220 package=THT]
  Arduino_NANO = Arduino Nano (Rev3.0)
  LAYER1-4 = mystery part, 4 pins [chip_label=?]
  LED1-8 = mystery part, 8 pins [chip_label=?]
  LED9-16 = mystery part, 8 pins [chip_label=?]
  5V = Header 2 [package=molex-1x2_lock]
  10uF = Electrolytic Capacitor [capacitance=1µF package="100 mil [THT, electrolytic]"]

nets:
  N1: 74HC595.Q1, ULN2003.In_6
  N2: 74HC595.Q2, ULN2003.In_5
  N3: 74HC595.Q3, ULN2003.In_4
  GND: 74HC595.GND, 74HC595_2.GND, 74HC595_3.GND, ULN2003.0V, Arduino_NANO.GND, 5V.2, 10uF.-
  N4: 74HC595.Q7', 74HC595_3.DS
  VCC: 74HC595.MR, 74HC595.VCC, 74HC595_2.MR, 74HC595_2.VCC, 74HC595_3.MR, 74HC595_3.VCC, Arduino_NANO.5V, 5V.1, 10uF.+
  N5: 74HC595.SH_CP, 74HC595_2.SH_CP, 74HC595_3.SH_CP, Arduino_NANO.D13/SCK
  N6: 74HC595.ST_CP, 74HC595_2.ST_CP, 74HC595_3.ST_CP, Arduino_NANO.D9
  N7: 74HC595.OE, 74HC595_2.OE, 74HC595_3.OE, Arduino_NANO.D10
  N8: 74HC595.DS, Arduino_NANO.D11/MOSI
  N9: 74HC595.Q0, ULN2003.In_7
  N10: 74HC595_2.Q1, R12.Pin_0
  N11: 74HC595_2.Q2, R11.Pin_0
  N12: 74HC595_2.Q3, R10.Pin_0
  N13: 74HC595_2.Q4, R9.Pin_0
  N14: 74HC595_2.Q5, R8.Pin_0
  N15: 74HC595_2.Q6, R7.Pin_0
  N16: 74HC595_2.Q7, R6.Pin_0
  N17: 74HC595_2.DS, 74HC595_3.Q7'
  N18: 74HC595_2.Q0, R3.Pin_0
  N19: 74HC595_3.Q1, R4.Pin_0
  N20: 74HC595_3.Q2, R19.Pin_0
  N21: 74HC595_3.Q3, R18.Pin_0
  N22: 74HC595_3.Q4, R17.Pin_0
  N23: 74HC595_3.Q5, R16.Pin_0
  N24: 74HC595_3.Q6, R15.Pin_0
  N25: 74HC595_3.Q7, R14.Pin_0
  N26: 74HC595_3.Q0, R2.Pin_0
  N27: R2.Pin_1, LED1-8.pin1
  N28: ULN2003.Out_7, LAYER1-4.pin1
  N29: ULN2003.Out_6, LAYER1-4.pin2
  N30: ULN2003.Out_5, LAYER1-4.pin3
  N31: ULN2003.Out_4, LAYER1-4.pin4
  N32: R3.Pin_1, LED9-16.pin1
  N33: R4.Pin_1, LED1-8.pin2
  N34: R6.Pin_1, LED9-16.pin8
  N35: R7.Pin_1, LED9-16.pin7
  N36: R8.Pin_1, LED9-16.pin6
  N37: R9.Pin_1, LED9-16.pin5
  N38: R10.Pin_1, LED9-16.pin4
  N39: R11.Pin_1, LED9-16.pin3
  N40: R12.Pin_1, LED9-16.pin2
  N41: R14.Pin_1, LED1-8.pin8
  N42: R15.Pin_1, LED1-8.pin7
  N43: R16.Pin_1, LED1-8.pin6
  N44: R17.Pin_1, LED1-8.pin5
  N45: R18.Pin_1, LED1-8.pin4
  N46: R19.Pin_1, LED1-8.pin3

notes:
  -
  USB
