# Fritzing sketch Arduino_4x4x4_LED_595_V2 (saved by Fritzing 0.9.3b)
circuit board: 10cm x 5cm
breadboards: 1

parts:
  LED9-17 = mystery part, 8 pins [chip_label=?]
  LED1-9 = mystery part, 8 pins [chip_label=?]
  Arduino_NANO1 = Arduino Nano (Rev3.0)
  U4 = 74HC595 [package="DIP16 [THT]"]
  U5 = 74HC595 [package="DIP16 [THT]"]
  U6 = 74HC595 [package="DIP16 [THT]"]
  R20 = Resistor [tolerance=±5% resistance=220 package=THT]
  R21 = Resistor [tolerance=±5% resistance=220 package=THT]
  R22 = Resistor [tolerance=±5% resistance=220 package=THT]
  R23 = Resistor [tolerance=±5% resistance=220 package=THT]
  R24 = Resistor [tolerance=±5% resistance=220 package=THT]
  R25 = Resistor [tolerance=±5% resistance=220 package=THT]
  R26 = Resistor [tolerance=±5% resistance=220 package=THT]
  R27 = Resistor [tolerance=±5% resistance=220 package=THT]
  R28 = Resistor [tolerance=±5% resistance=220 package=THT]
  R29 = Resistor [tolerance=±5% resistance=220 package=THT]
  R30 = Resistor [tolerance=±5% resistance=220 package=THT]
  R31 = Resistor [tolerance=±5% resistance=220 package=THT]
  R32 = Resistor [tolerance=±5% resistance=220 package=THT]
  R33 = Resistor [tolerance=±5% resistance=220 package=THT]
  R34 = Resistor [tolerance=±5% resistance=220 package=THT]
  R35 = Resistor [tolerance=±5% resistance=220 package=THT]
  ULN2804 = ULN2803 Darlington Array
  LAYER1-4 = mystery part, 4 pins [chip_label=?]

nets:
  N1: LED9-17.pin1, R34.Pin_1
  N2: LED9-17.pin2, R26.Pin_1
  N3: LED9-17.pin3, R27.Pin_1
  N4: LED9-17.pin4, R28.Pin_1
  N5: LED9-17.pin5, R29.Pin_1
  N6: LED9-17.pin6, R30.Pin_1
  N7: LED9-17.pin7, R31.Pin_1
  N8: LED9-17.pin8, R32.Pin_1
  N9: LED1-9.pin1, R35.Pin_1
  N10: LED1-9.pin2, R33.Pin_1
  N11: LED1-9.pin3, R20.Pin_1
  N12: LED1-9.pin4, R21.Pin_1
  N13: LED1-9.pin5, R22.Pin_1
  N14: LED1-9.pin6, R23.Pin_1
  N15: LED1-9.pin7, R24.Pin_1
  N16: LED1-9.pin8, R25.Pin_1
  GND: Arduino_NANO1.GND, U4.GND, U5.GND, U6.GND, ULN2804.GND
  N17: Arduino_NANO1.D9, U4.ST_CP, U5.ST_CP, U6.ST_CP
  N18: Arduino_NANO1.D10, U4.OE, U5.OE, U6.OE
  N19: Arduino_NANO1.D11/MOSI, U6.DS
  VCC: Arduino_NANO1.5V, U4.MR, U4.VCC, U5.MR, U5.VCC, U6.MR, U6.VCC
  N20: Arduino_NANO1.D13/SCK, U4.SH_CP, U5.SH_CP, U6.SH_CP
  N21: U4.Q1, R33.Pin_0
  N22: U4.Q2, R20.Pin_0
  N23: U4.Q3, R21.Pin_0
  N24: U4.Q4, R22.Pin_0
  N25: U4.Q5, R23.Pin_0
  N26: U4.Q6, R24.Pin_0
  N27: U4.Q7, R25.Pin_0
  N28: U4.Q7', U5.DS
  N29: U4.DS, U6.Q7'
  N30: U4.Q0, R35.Pin_0
  N31: U5.Q1, R26.Pin_0
  N32: U5.Q2, R27.Pin_0
  N33: U5.Q3, R28.Pin_0
  N34: U5.Q4, R29.Pin_0
  N35: U5.Q5, R30.Pin_0
  N36: U5.Q6, R31.Pin_0
  N37: U5.Q7, R32.Pin_0
  N38: U5.Q0, R34.Pin_0
  N39: U6.Q1, ULN2804.I7
  N40: U6.Q2, ULN2804.I6
  N41: U6.Q3, ULN2804.I5
  N42: U6.Q0, ULN2804.I8
  N43: ULN2804.O8, LAYER1-4.pin1
  N44: ULN2804.O7, LAYER1-4.pin2
  N45: ULN2804.O6, LAYER1-4.pin3
  N46: ULN2804.O5, LAYER1-4.pin4

notes:
  ULN2803
  74HC595
  USB
  C

custom parts:
  ULN2803 Darlington Array: ULN2803 Darlington Transistor Array with Flyback Protection
