# Fritzing sketch _4x4x4_RGB_595_v5 (saved by Fritzing 0.9.3b)
circuit board: 12.9cm x 10cm

parts:
  U1 = 74HC595 [package="DIP16 [THT]"]
  U2 = 74HC595 [package="DIP16 [THT]"]
  U3 = 74HC595 [package="DIP16 [THT]"]
  R2 = Resistor [tolerance=±5% resistance=220 package=THT]
  R3 = Resistor [tolerance=±5% resistance=220 package=THT]
  R4 = Resistor [tolerance=±5% resistance=220 package=THT]
  R6 = Resistor [tolerance=±5% resistance=220 package=THT]
  R7 = Resistor [tolerance=±5% resistance=220 package=THT]
  R8 = Resistor [tolerance=±5% resistance=220 package=THT]
  R9 = Resistor [tolerance=±5% resistance=220 package=THT]
  R10 = Resistor [tolerance=±5% resistance=220 package=THT]
  R11 = Resistor [tolerance=±5% resistance=220 package=THT]
  R12 = Resistor [tolerance=±5% resistance=220 package=THT]
  R14 = Resistor [tolerance=±5% resistance=220 package=THT]
  R15 = Resistor [tolerance=±5% resistance=220 package=THT]
  R16 = Resistor [tolerance=±5% resistance=220 package=THT]
  R17 = Resistor [tolerance=±5% resistance=220 package=THT]
  R18 = Resistor [tolerance=±5% resistance=220 package=THT]
  R19 = Resistor [tolerance=±5% resistance=220 package=THT]
  U6 = 74HC595 [package="DIP16 [THT]"]
  R36 = Resistor [tolerance=±5% resistance=220 package=THT]
  R37 = Resistor [tolerance=±5% resistance=220 package=THT]
  R38 = Resistor [tolerance=±5% resistance=220 package=THT]
  R39 = Resistor [tolerance=±5% resistance=220 package=THT]
  R40 = Resistor [tolerance=±5% resistance=220 package=THT]
  R41 = Resistor [tolerance=±5% resistance=220 package=THT]
  R42 = Resistor [tolerance=±5% resistance=220 package=THT]
  R43 = Resistor [tolerance=±5% resistance=220 package=THT]
  U7 = 74HC595 [package="DIP16 [THT]"]
  R44 = Resistor [tolerance=±5% resistance=220 package=THT]
  R45 = Resistor [tolerance=±5% resistance=220 package=THT]
  R46 = Resistor [tolerance=±5% resistance=220 package=THT]
  R47 = Resistor [tolerance=±5% resistance=220 package=THT]
  R48 = Resistor [tolerance=±5% resistance=220 package=THT]
  R49 = Resistor [tolerance=±5% resistance=220 package=THT]
  R50 = Resistor [tolerance=±5% resistance=220 package=THT]
  R51 = Resistor [tolerance=±5% resistance=220 package=THT]
  U8 = 74HC595 [package="DIP16 [THT]"]
  R52 = Resistor [tolerance=±5% resistance=220 package=THT]
  R53 = Resistor [tolerance=±5% resistance=220 package=THT]
  R54 = Resistor [tolerance=±5% resistance=220 package=THT]
  R55 = Resistor [tolerance=±5% resistance=220 package=THT]
  R56 = Resistor [tolerance=±5% resistance=220 package=THT]
  R57 = Resistor [tolerance=±5% resistance=220 package=THT]
  R58 = Resistor [tolerance=±5% resistance=220 package=THT]
  R59 = Resistor [tolerance=±5% resistance=220 package=THT]
  U9 = 74HC595 [package="DIP16 [THT]"]
  R60 = Resistor [tolerance=±5% resistance=220 package=THT]
  R61 = Resistor [tolerance=±5% resistance=220 package=THT]
  R62 = Resistor [tolerance=±5% resistance=220 package=THT]
  R63 = Resistor [tolerance=±5% resistance=220 package=THT]
  R64 = Resistor [tolerance=±5% resistance=220 package=THT]
  R65 = Resistor [tolerance=±5% resistance=220 package=THT]
  R66 = Resistor [tolerance=±5% resistance=220 package=THT]
  R67 = Resistor [tolerance=±5% resistance=220 package=THT]
  J1 = screw terminal, 2 pins
  Arduino_NANO = Arduino Nano (Rev3.0)
  RED1 = mystery part, 8 pins [chip_label=?]
  RED2 = mystery part, 8 pins [chip_label=?]
  GREEN1 = mystery part, 8 pins [chip_label=?]
  GREEN2 = mystery part, 8 pins [chip_label=?]
  BLUE1 = mystery part, 8 pins [chip_label=?]
  BLUE2 = mystery part, 8 pins [chip_label=?]
  10uF = Electrolytic Capacitor [capacitance=10µF voltage=10V package="200 mil [THT, electrolytic]"]
  RB1 = Resistor [tolerance=±5% resistance=100 package=THT]
  RB2 = Resistor [tolerance=±5% resistance=100 package=THT]
  RB3 = Resistor [tolerance=±5% resistance=100 package=THT]
  RB4 = Resistor [tolerance=±5% resistance=100 package=THT]
  Q1 = Basic FET P-Channel [package="TO220 [THT]"]
  ULN2003 = ULN2003A [package="DIP16 [THT]"]
  Q2 = Basic FET P-Channel [package="TO220 [THT]"]
  Q3 = Basic FET P-Channel [package="TO220 [THT]"]
  Q4 = Basic FET P-Channel [package="TO220 [THT]"]
  ULN2803-1 = ULN2803A [package=THT]
  ULN2803-2 = ULN2803A [package=THT]
  ULN2803-3 = ULN2803A [package=THT]
  ULN2803-4 = ULN2803A [package=THT]
  ULN2803-5 = ULN2803A [package=THT]
  ULN2803-6 = ULN2803A [package=THT]
  5V = Header 2 [package=molex-1x2_lock]
  3-4 = Header 2 [package=molex-1x2_lock]
  1-2 = Header 2 [package=molex-1x2_lock]

nets:
  N1: U1.Q1, ULN2003.In_6
  N2: U1.Q2, ULN2003.In_5
  N3: U1.Q3, ULN2003.In_4
  GND: U1.GND, U2.GND, U3.GND, U6.GND, U7.GND, U8.GND, U9.GND, J1.pin1, Arduino_NANO.GND, 10uF.-, ULN2003.0V, ULN2803-1.0V, ULN2803-2.0V, ULN2803-3.0V, ULN2803-4.0V, ULN2803-5.0V, ULN2803-6.0V, 5V.1
  N4: U1.Q7', U3.DS
  VCC: U1.MR, U1.VCC, U2.MR, U2.VCC, U3.MR, U3.VCC, U6.MR, U6.VCC, U7.MR, U7.VCC, U8.MR, U8.VCC, U9.MR, U9.VCC, J1.pin2, Arduino_NANO.5V, 10uF.+, RB1.Pin_1, RB2.Pin_1, RB3.Pin_1, RB4.Pin_1, Q1.source, Q2.source, Q3.source, Q4.source, 5V.2
  N5: U1.SH_CP, U2.SH_CP, U3.SH_CP, U6.SH_CP, U7.SH_CP, U8.SH_CP, U9.SH_CP, Arduino_NANO.D13/SCK
  N6: U1.ST_CP, U2.ST_CP, U3.ST_CP, U6.ST_CP, U7.ST_CP, U8.ST_CP, U9.ST_CP, Arduino_NANO.D9
  N7: U1.OE, U2.OE, U3.OE, U6.OE, U7.OE, U8.OE, U9.OE, Arduino_NANO.D10
  N8: U1.DS, Arduino_NANO.D11/MOSI
  N9: U1.Q0, ULN2003.In_7
  N10: U2.Q1, ULN2803-2.In_7
  N11: U2.Q2, ULN2803-2.In_6
  N12: U2.Q3, ULN2803-2.In_5
  N13: U2.Q4, ULN2803-2.In_4
  N14: U2.Q5, ULN2803-2.In_3
  N15: U2.Q6, ULN2803-2.In_2
  N16: U2.Q7, ULN2803-2.In_1
  N17: U2.Q7', U6.DS
  N18: U2.DS, U3.Q7'
  N19: U2.Q0, ULN2803-2.In_8
  N20: U3.Q1, ULN2803-1.In_7
  N21: U3.Q2, ULN2803-1.In_6
  N22: U3.Q3, ULN2803-1.In_5
  N23: U3.Q4, ULN2803-1.In_4
  N24: U3.Q5, ULN2803-1.In_3
  N25: U3.Q6, ULN2803-1.In_2
  N26: U3.Q7, ULN2803-1.In_1
  N27: U3.Q0, ULN2803-1.In_8
  N28: R2.Pin_0, ULN2803-1.Out_8
  N29: R2.Pin_1, RED1.pin1
  N30: R3.Pin_0, ULN2803-2.Out_8
  N31: R3.Pin_1, RED2.pin1
  N32: R4.Pin_0, ULN2803-1.Out_7
  N33: R4.Pin_1, RED1.pin2
  N34: R6.Pin_0, ULN2803-2.Out_1
  N35: R6.Pin_1, RED2.pin8
  N36: R7.Pin_0, ULN2803-2.Out_2
  N37: R7.Pin_1, RED2.pin7
  N38: R8.Pin_0, ULN2803-2.Out_3
  N39: R8.Pin_1, RED2.pin6
  N40: R9.Pin_0, ULN2803-2.Out_4
  N41: R9.Pin_1, RED2.pin5
  N42: R10.Pin_0, ULN2803-2.Out_5
  N43: R10.Pin_1, RED2.pin4
  N44: R11.Pin_0, ULN2803-2.Out_6
  N45: R11.Pin_1, RED2.pin3
  N46: R12.Pin_0, ULN2803-2.Out_7
  N47: R12.Pin_1, RED2.pin2
  N48: R14.Pin_0, ULN2803-1.Out_1
  N49: R14.Pin_1, RED1.pin8
  N50: R15.Pin_0, ULN2803-1.Out_2
  N51: R15.Pin_1, RED1.pin7
  N52: R16.Pin_0, ULN2803-1.Out_3
  N53: R16.Pin_1, RED1.pin6
  N54: R17.Pin_0, ULN2803-1.Out_4
  N55: R17.Pin_1, RED1.pin5
  N56: R18.Pin_0, ULN2803-1.Out_5
  N57: R18.Pin_1, RED1.pin4
  N58: R19.Pin_0, ULN2803-1.Out_6
  N59: R19.Pin_1, RED1.pin3
  N60: U6.Q1, ULN2803-3.In_7
  N61: U6.Q2, ULN2803-3.In_6
  N62: U6.Q3, ULN2803-3.In_5
  N63: U6.Q4, ULN2803-3.In_4
  N64: U6.Q5, ULN2803-3.In_3
  N65: U6.Q6, ULN2803-3.In_2
  N66: U6.Q7, ULN2803-3.In_1
  N67: U6.Q7', U7.DS
  N68: U6.Q0, ULN2803-3.In_8
  N69: R36.Pin_0, ULN2803-3.Out_7
  N70: R36.Pin_1, GREEN1.pin7
  N71: R37.Pin_0, ULN2803-3.Out_6
  N72: R37.Pin_1, GREEN1.pin6
  N73: R38.Pin_0, ULN2803-3.Out_5
  N74: R38.Pin_1, GREEN1.pin5
  N75: R39.Pin_0, ULN2803-3.Out_4
  N76: R39.Pin_1, GREEN1.pin4
  N77: R40.Pin_0, ULN2803-3.Out_3
  N78: R40.Pin_1, GREEN1.pin3
  N79: R41.Pin_0, ULN2803-3.Out_2
  N80: R41.Pin_1, GREEN1.pin2
  N81: R42.Pin_0, ULN2803-3.Out_1
  N82: R42.Pin_1, GREEN1.pin1
  N83: R43.Pin_0, ULN2803-3.Out_8
  N84: R43.Pin_1, GREEN1.pin8
  N85: U7.Q1, ULN2803-4.In_7
  N86: U7.Q2, ULN2803-4.In_6
  N87: U7.Q3, ULN2803-4.In_5
  N88: U7.Q4, ULN2803-4.In_4
  N89: U7.Q5, ULN2803-4.In_3
  N90: U7.Q6, ULN2803-4.In_2
  N91: U7.Q7, ULN2803-4.In_1
  N92: U7.Q7', U8.DS
  N93: U7.Q0, ULN2803-4.In_8
  N94: R44.Pin_0, ULN2803-4.Out_7
  N95: R44.Pin_1, GREEN2.pin7
  N96: R45.Pin_0, ULN2803-4.Out_6
  N97: R45.Pin_1, GREEN2.pin6
  N98: R46.Pin_0, ULN2803-4.Out_5
  N99: R46.Pin_1, GREEN2.pin5
  N100: R47.Pin_0, ULN2803-4.Out_4
  N101: R47.Pin_1, GREEN2.pin4
  N102: R48.Pin_0, ULN2803-4.Out_3
  N103: R48.Pin_1, GREEN2.pin3
  N104: R49.Pin_0, ULN2803-4.Out_2
  N105: R49.Pin_1, GREEN2.pin2
  N106: R50.Pin_0, ULN2803-4.Out_1
  N107: R50.Pin_1, GREEN2.pin1
  N108: R51.Pin_0, ULN2803-4.Out_8
  N109: R51.Pin_1, GREEN2.pin8
  N110: U8.Q1, ULN2803-5.In_7
  N111: U8.Q2, ULN2803-5.In_6
  N112: U8.Q3, ULN2803-5.In_5
  N113: U8.Q4, ULN2803-5.In_4
  N114: U8.Q5, ULN2803-5.In_3
  N115: U8.Q6, ULN2803-5.In_2
  N116: U8.Q7, ULN2803-5.In_1
  N117: U8.Q7', U9.DS
  N118: U8.Q0, ULN2803-5.In_8
  N119: R52.Pin_0, ULN2803-5.Out_7
  N120: R52.Pin_1, BLUE1.pin7
  N121: R53.Pin_0, ULN2803-5.Out_6
  N122: R53.Pin_1, BLUE1.pin6
  N123: R54.Pin_0, ULN2803-5.Out_5
  N124: R54.Pin_1, BLUE1.pin5
  N125: R55.Pin_0, ULN2803-5.Out_4
  N126: R55.Pin_1, BLUE1.pin4
  N127: R56.Pin_0, ULN2803-5.Out_3
  N128: R56.Pin_1, BLUE1.pin3
  N129: R57.Pin_0, ULN2803-5.Out_2
  N130: R57.Pin_1, BLUE1.pin2
  N131: R58.Pin_0, ULN2803-5.Out_1
  N132: R58.Pin_1, BLUE1.pin1
  N133: R59.Pin_0, ULN2803-5.Out_8
  N134: R59.Pin_1, BLUE1.pin8
  N135: U9.Q1, ULN2803-6.In_7
  N136: U9.Q2, ULN2803-6.In_6
  N137: U9.Q3, ULN2803-6.In_5
  N138: U9.Q4, ULN2803-6.In_4
  N139: U9.Q5, ULN2803-6.In_3
  N140: U9.Q6, ULN2803-6.In_2
  N141: U9.Q7, ULN2803-6.In_1
  N142: U9.Q0, ULN2803-6.In_8
  N143: R60.Pin_0, ULN2803-6.Out_7
  N144: R60.Pin_1, BLUE2.pin7
  N145: R61.Pin_0, ULN2803-6.Out_6
  N146: R61.Pin_1, BLUE2.pin6
  N147: R62.Pin_0, ULN2803-6.Out_5
  N148: R62.Pin_1, BLUE2.pin5
  N149: R63.Pin_0, ULN2803-6.Out_4
  N150: R63.Pin_1, BLUE2.pin4
  N151: R64.Pin_0, ULN2803-6.Out_3
  N152: R64.Pin_1, BLUE2.pin3
  N153: R65.Pin_0, ULN2803-6.Out_2
  N154: R65.Pin_1, BLUE2.pin2
  N155: R66.Pin_0, ULN2803-6.Out_1
  N156: R66.Pin_1, BLUE2.pin1
  N157: R67.Pin_0, ULN2803-6.Out_8
  N158: R67.Pin_1, BLUE2.pin8
  N159: RB1.Pin_0, Q1.gate, ULN2003.Out_4
  N160: RB2.Pin_0, ULN2003.Out_5, Q2.gate
  N161: RB3.Pin_0, ULN2003.Out_6, Q3.gate
  N162: RB4.Pin_0, ULN2003.Out_7, Q4.gate
  N163: Q1.drain, 1-2.2
  N164: Q2.drain, 1-2.1
  N165: Q3.drain, 3-4.2
  N166: Q4.drain, 3-4.1

notes:
  -
  5V
  +++ 5V +++
  GND
  C
  C1
  USB
  74HC595
  R1-R48 330-500
  C - 100nF
  RGB 4x4x4 LED CUBE
  Bakisha2018
