# Fritzing sketch Arduino_7x7x7_LED_595_V1.1 (saved by Fritzing 0.9.3b)
circuit board: 15cm x 10cm
breadboards: 1

parts:
  U1 = 74HC595 [package="DIP16 [THT]"]
  U2 = 74HC595 [package="DIP16 [THT]"]
  U3 = 74HC595 [package="DIP16 [THT]"]
  C1 = Ceramic Capacitor [capacitance=100nF package="200 mil [THT, multilayer]"]
  C2 = Ceramic Capacitor [capacitance=100nF package="200 mil [THT, multilayer]"]
  C3 = Ceramic Capacitor [capacitance=100nF package="200 mil [THT, multilayer]"]
  R2 = Resistor [tolerance=±5% resistance=100 package=THT]
  R3 = Resistor [tolerance=±5% resistance=100 package=THT]
  R11 = Resistor [tolerance=±5% resistance=100 package=THT]
  R12 = Resistor [tolerance=±5% resistance=100 package=THT]
  R13 = Resistor [tolerance=±5% resistance=100 package=THT]
  R14 = Resistor [tolerance=±5% resistance=100 package=THT]
  R15 = Resistor [tolerance=±5% resistance=100 package=THT]
  R16 = Resistor [tolerance=±5% resistance=100 package=THT]
  R17 = Resistor [tolerance=±5% resistance=100 package=THT]
  R18 = Resistor [tolerance=±5% resistance=100 package=THT]
  R19 = Resistor [tolerance=±5% resistance=100 package=THT]
  R20 = Resistor [tolerance=±5% resistance=100 package=THT]
  R21 = Resistor [tolerance=±5% resistance=100 package=THT]
  R22 = Resistor [tolerance=±5% resistance=100 package=THT]
  R23 = Resistor [tolerance=±5% resistance=100 package=THT]
  R24 = Resistor [tolerance=±5% resistance=100 package=THT]
  U5 = 74HC595 [package="DIP16 [THT]"]
  U6 = 74HC595 [package="DIP16 [THT]"]
  C4 = Ceramic Capacitor [capacitance=100nF package="200 mil [THT, multilayer]"]
  C6 = Ceramic Capacitor [capacitance=100nF package="200 mil [THT, multilayer]"]
  R25 = Resistor [tolerance=±5% resistance=100 package=THT]
  R28 = Resistor [tolerance=±5% resistance=100 package=THT]
  R30 = Resistor [tolerance=±5% resistance=100 package=THT]
  R31 = Resistor [tolerance=±5% resistance=100 package=THT]
  R32 = Resistor [tolerance=±5% resistance=100 package=THT]
  R33 = Resistor [tolerance=±5% resistance=100 package=THT]
  R34 = Resistor [tolerance=±5% resistance=100 package=THT]
  R35 = Resistor [tolerance=±5% resistance=100 package=THT]
  R37 = Resistor [tolerance=±5% resistance=100 package=THT]
  R38 = Resistor [tolerance=±5% resistance=100 package=THT]
  R39 = Resistor [tolerance=±5% resistance=100 package=THT]
  R41 = Resistor [tolerance=±5% resistance=100 package=THT]
  R44 = Resistor [tolerance=±5% resistance=100 package=THT]
  R46 = Resistor [tolerance=±5% resistance=100 package=THT]
  R47 = Resistor [tolerance=±5% resistance=100 package=THT]
  R48 = Resistor [tolerance=±5% resistance=100 package=THT]
  U10 = 74HC595 [package="DIP16 [THT]"]
  U11 = 74HC595 [package="DIP16 [THT]"]
  C9 = Ceramic Capacitor [capacitance=100nF package="200 mil [THT, multilayer]"]
  C11 = Ceramic Capacitor [capacitance=100nF package="200 mil [THT, multilayer]"]
  R49 = Resistor [tolerance=±5% resistance=100 package=THT]
  R54 = Resistor [tolerance=±5% resistance=100 package=THT]
  R57 = Resistor [tolerance=±5% resistance=100 package=THT]
  R60 = Resistor [tolerance=±5% resistance=100 package=THT]
  R62 = Resistor [tolerance=±5% resistance=100 package=THT]
  R66 = Resistor [tolerance=±5% resistance=100 package=THT]
  R67 = Resistor [tolerance=±5% resistance=100 package=THT]
  R68 = Resistor [tolerance=±5% resistance=100 package=THT]
  R72 = Resistor [tolerance=±5% resistance=100 package=THT]
  R74 = Resistor [tolerance=±5% resistance=100 package=THT]
  R76 = Resistor [tolerance=±5% resistance=100 package=THT]
  R80 = Resistor [tolerance=±5% resistance=100 package=THT]
  R81 = Resistor [tolerance=±5% resistance=100 package=THT]
  R83 = Resistor [tolerance=±5% resistance=100 package=THT]
  R85 = Resistor [tolerance=±5% resistance=100 package=THT]
  R87 = Resistor [tolerance=±5% resistance=100 package=THT]
  JP1 = Header 1 [package=1x01_offset]
  JP2 = Header 1 [package=1x01_offset]
  JP3 = Header 1 [package=1x01_offset]
  JP4 = Header 1 [package=1x01_offset]
  JP6 = Header 1 [package=1x01_offset]
  JP7 = Header 1 [package=1x01_offset]
  JP8 = Header 1 [package=1x01_offset]
  JP9 = Header 1 [package=1x01_offset]
  JP10 = Header 1 [package=1x01_offset]
  JP11 = Header 1 [package=1x01_offset]
  JP12 = Header 1 [package=1x01_offset]
  JP13 = Header 1 [package=1x01_offset]
  JP14 = Header 1 [package=1x01_offset]
  JP15 = Header 1 [package=1x01_offset]
  JP16 = Header 1 [package=1x01_offset]
  JP17 = Header 1 [package=1x01_offset]
  JP18 = Header 1 [package=1x01_offset]
  JP19 = Header 1 [package=1x01_offset]
  JP20 = Header 1 [package=1x01_offset]
  JP21 = Header 1 [package=1x01_offset]
  JP22 = Header 1 [package=1x01_offset]
  JP23 = Header 1 [package=1x01_offset]
  JP24 = Header 1 [package=1x01_offset]
  JP25 = Header 1 [package=1x01_offset]
  JP26 = Header 1 [package=1x01_offset]
  JP27 = Header 1 [package=1x01_offset]
  JP28 = Header 1 [package=1x01_offset]
  JP29 = Header 1 [package=1x01_offset]
  JP30 = Header 1 [package=1x01_offset]
  JP31 = Header 1 [package=1x01_offset]
  JP32 = Header 1 [package=1x01_offset]
  JP33 = Header 1 [package=1x01_offset]
  JP34 = Header 1 [package=1x01_offset]
  JP35 = Header 1 [package=1x01_offset]
  JP37 = Header 1 [package=1x01_offset]
  JP38 = Header 1 [package=1x01_offset]
  JP39 = Header 1 [package=1x01_offset]
  JP40 = Header 1 [package=1x01_offset]
  JP41 = Header 1 [package=1x01_offset]
  JP44 = Header 1 [package=1x01_offset]
  JP46 = Header 1 [package=1x01_offset]
  JP48 = Header 1 [package=1x01_offset]
  JP50 = Header 1 [package=1x01_offset]
  JP52 = Header 1 [package=1x01_offset]
  JP56 = Header 1 [package=1x01_offset]
  JP57 = Header 1 [package=1x01_offset]
  JP59 = Header 1 [package=1x01_offset]
  JP61 = Header 1 [package=1x01_offset]
  JP67 = Header 1 [package=1x01_offset]
  JP68 = Header 1 [package=1x01_offset]
  JP71 = Header 1 [package=1x01_offset]
  JP72 = Header 1 [package=1x01_offset]
  JP74 = Header 1 [package=1x01_offset]
  JP78 = Header 1 [package=1x01_offset]
  IC1 = ULN2003A [package="DIP16 [THT]"]
  Nano1 = Arduino Nano v2.3
  J1 = Power Jack [package=power_jack_slot]
  JP79 = Header 1 [package=1x01_offset]
  JP80 = Header 1 [package=1x01_offset]
  JP81 = Header 1 [package=1x01_offset]
  JP82 = Header 1 [package=1x01_offset]
  JP83 = Header 1 [package=1x01_offset]
  JP84 = Header 1 [package=1x01_offset]
  JP85 = Header 1 [package=1x01_offset]
  JP86 = Header 1 [package=1x01_offset]
  JP87 = Header 1 [package=1x01_offset]
  JP88 = Header 1 [package=1x01_offset]
  LM1 = RioRand LM2596
  in+ = Header 1 [package=1x01_offset]
  in- = Header 1 [package=1x01_offset]
  out- = Header 1 [package=1x01_offset]
  out+ = Header 1 [package=1x01_offset]
  U12 = 74HC595 [package="DIP16 [THT]"]
  R88 = Resistor [tolerance=±5% resistance=100 package=THT]
  JP89 = Header 1 [package=1x01_offset]
  JP90 = Header 1 [package=1x01_offset]
  C12 = Ceramic Capacitor [capacitance=100nF package="200 mil [THT, multilayer]"]

nets:
  N1: U1.Q1, IC1.In_6
  N2: U1.Q2, IC1.In_5
  N3: U1.Q3, IC1.In_4
  N4: U1.Q4, IC1.In_3
  N5: U1.Q5, IC1.In_2
  N6: U1.Q6, IC1.In_1
  GND: U1.GND, U2.GND, U3.GND, C1.0, C2.0, C3.0, U5.GND, U6.GND, C4.0, C6.0, U10.GND, U11.GND, C9.0, C11.0, IC1.0V, Nano1.GND, LM1.Pin_3, out-.1, U12.GND, C12.0
  N7: U1.Q7', U2.DS
  VCC: U1.MR, U1.VCC, U2.MR, U2.VCC, U3.MR, U3.VCC, C1.1, C2.1, C3.1, U5.MR, U5.VCC, U6.MR, U6.VCC, C4.1, C6.1, U10.MR, U10.VCC, U11.MR, U11.VCC, C9.1, C11.1, Nano1.VIN, LM1.Pin_2, out+.1, U12.MR, U12.VCC, C12.1
  N8: U1.SH_CP, U2.SH_CP, U3.SH_CP, U5.SH_CP, U6.SH_CP, U10.SH_CP, U11.SH_CP, Nano1.D13, U12.SH_CP
  N9: U1.ST_CP, U2.ST_CP, U3.ST_CP, U5.ST_CP, U6.ST_CP, U10.ST_CP, U11.ST_CP, Nano1.D10, U12.ST_CP
  N10: U1.OE, U2.OE, U3.OE, U5.OE, U6.OE, U10.OE, U11.OE, Nano1.D9, U12.OE
  N11: U1.DS, Nano1.D11
  N12: U1.Q0, IC1.In_7
  N13: U2.Q1, R11.Pin_1
  N14: U2.Q2, R12.Pin_1
  N15: U2.Q3, R14.Pin_1
  N16: U2.Q4, R17.Pin_1
  N17: U2.Q5, R16.Pin_1
  N18: U2.Q6, R15.Pin_1
  N19: U2.Q7, R13.Pin_1
  N20: U2.Q7', U3.DS
  N21: U2.Q0, R2.Pin_1
  N22: U3.Q1, R23.Pin_1
  N23: U3.Q2, R21.Pin_1
  N24: U3.Q3, R20.Pin_1
  N25: U3.Q4, R24.Pin_1
  N26: U3.Q5, R22.Pin_1
  N27: U3.Q6, R18.Pin_1
  N28: U3.Q7, R19.Pin_1
  N29: U3.Q7', U6.DS
  N30: U3.Q0, R3.Pin_1
  N31: R2.Pin_0, JP31.1
  N32: R3.Pin_0, JP19.1
  N33: R11.Pin_0, JP28.1
  N34: R12.Pin_0, JP25.1
  N35: R13.Pin_0, JP30.1
  N36: R14.Pin_0, JP29.1
  N37: R15.Pin_0, JP27.1
  N38: R16.Pin_0, JP26.1
  N39: R17.Pin_0, JP32.1
  N40: R18.Pin_0, JP21.1
  N41: R19.Pin_0, JP24.1
  N42: R20.Pin_0, JP20.1
  N43: R21.Pin_0, JP17.1
  N44: R22.Pin_0, JP23.1
  N45: R23.Pin_0, JP22.1
  N46: R24.Pin_0, JP18.1
  N47: U5.Q1, R31.Pin_1
  N48: U5.Q2, R32.Pin_1
  N49: U5.Q3, R33.Pin_1
  N50: U5.Q4, R38.Pin_1
  N51: U5.Q5, R35.Pin_1
  N52: U5.Q6, R30.Pin_1
  N53: U5.Q7, R25.Pin_1
  N54: U5.Q7', U11.DS
  N55: U5.DS, U6.Q7'
  N56: U5.Q0, R47.Pin_1
  N57: U6.Q1, R44.Pin_1
  N58: U6.Q2, R28.Pin_1
  N59: U6.Q3, R37.Pin_1
  N60: U6.Q4, R48.Pin_1
  N61: U6.Q5, R34.Pin_1
  N62: U6.Q6, R46.Pin_1
  N63: U6.Q7, R39.Pin_1
  N64: U6.Q0, R41.Pin_1
  N65: R25.Pin_0, JP1.1
  N66: R28.Pin_0, JP10.1
  N67: R30.Pin_0, JP2.1
  N68: R31.Pin_0, JP8.1
  N69: R32.Pin_0, JP7.1
  N70: R33.Pin_0, JP90.1
  N71: R34.Pin_0, JP13.1
  N72: R35.Pin_0, JP4.1
  N73: R37.Pin_0, JP16.1
  N74: R38.Pin_0, JP3.1
  N75: R39.Pin_0, JP12.1
  N76: R41.Pin_0, JP11.1
  N77: R44.Pin_0, JP14.1
  N78: R46.Pin_0, JP15.1
  N79: R47.Pin_0, JP6.1
  N80: R48.Pin_0, JP9.1
  N81: U10.Q1, R67.Pin_1
  N82: U10.Q2, R57.Pin_1
  N83: U10.Q3, R83.Pin_1
  N84: U10.Q4, R68.Pin_1
  N85: U10.Q5, R49.Pin_1
  N86: U10.Q6, R62.Pin_1
  N87: U10.Q7, R74.Pin_1
  N88: U10.Q7', U12.DS
  N89: U10.DS, U11.Q7'
  N90: U10.Q0, R85.Pin_1
  N91: U11.Q1, R87.Pin_1
  N92: U11.Q2, R76.Pin_1
  N93: U11.Q3, R54.Pin_1
  N94: U11.Q4, R60.Pin_1
  N95: U11.Q5, R66.Pin_1
  N96: U11.Q6, R81.Pin_1
  N97: U11.Q7, R72.Pin_1
  N98: U11.Q0, R80.Pin_1
  N99: R49.Pin_0, JP72.1
  N100: R54.Pin_0, JP44.1
  N101: R57.Pin_0, JP46.1
  N102: R60.Pin_0, JP68.1
  N103: R62.Pin_0, JP57.1
  N104: R66.Pin_0, JP71.1
  N105: R67.Pin_0, JP50.1
  N106: R68.Pin_0, JP41.1
  N107: R72.Pin_0, JP52.1
  N108: R74.Pin_0, JP59.1
  N109: R76.Pin_0, JP56.1
  N110: R80.Pin_0, JP48.1
  N111: R81.Pin_0, JP74.1
  N112: R83.Pin_0, JP61.1
  N113: R85.Pin_0, JP78.1
  N114: R87.Pin_0, JP67.1
  N115: JP33.1, IC1.Out_5
  N116: JP34.1, IC1.Out_7
  N117: JP35.1, IC1.Out_6
  N118: JP37.1, IC1.Out_4
  N119: JP38.1, IC1.Out_3
  N120: JP39.1, IC1.Out_1
  N121: JP40.1, IC1.Out_2
  N122: Nano1.D2, JP82.1
  N123: Nano1.D3, JP83.1
  N124: Nano1.D4, JP84.1
  N125: Nano1.D5, JP85.1
  N126: Nano1.D6, JP88.1
  N127: Nano1.D7, JP87.1
  N128: Nano1.D8, JP86.1
  N129: Nano1.A2, JP81.1
  N130: Nano1.A1, JP79.1
  N131: Nano1.A0, JP80.1
  N132: J1.GND, LM1.Pin_1, in-.1
  N133: J1.PWR, LM1.Pin_0, in+.1
  N134: U12.Q0, R88.Pin_1
  N135: R88.Pin_0, JP89.1
