# Fritzing sketch 8x8x8_V2 (saved by Fritzing 0.9.3b)
circuit board: 15cm x 10cm

parts:
  U1 = 74HC595 [package="DIP16 [THT]"]
  U2 = 74HC595 [package="DIP16 [THT]"]
  U3 = 74HC595 [package="DIP16 [THT]"]
  R2 = Resistor [tolerance=±5% resistance=220 package=THT]
  R3 = Resistor [tolerance=±5% resistance=220 package=THT]
  R4 = Resistor [tolerance=±5% resistance=220 package=THT]
  R6 = Resistor [tolerance=±5% resistance=220 package=THT]
  R7 = Resistor [tolerance=±5% resistance=220 package=THT]
  R8 = Resistor [tolerance=±5% resistance=220 package=THT]
  R9 = Resistor [tolerance=±5% resistance=220 package=THT]
  R10 = Resistor [tolerance=±5% resistance=220 package=THT]
  R11 = Resistor [tolerance=±5% resistance=220 package=THT]
  R12 = Resistor [tolerance=±5% resistance=220 package=THT]
  R14 = Resistor [tolerance=±5% resistance=220 package=THT]
  R15 = Resistor [tolerance=±5% resistance=220 package=THT]
  R16 = Resistor [tolerance=±5% resistance=220 package=THT]
  R17 = Resistor [tolerance=±5% resistance=220 package=THT]
  R18 = Resistor [tolerance=±5% resistance=220 package=THT]
  R19 = Resistor [tolerance=±5% resistance=220 package=THT]
  ULN2803 = ULN2803 Darlington Array
  U4 = 74HC595 [package="DIP16 [THT]"]
  R20 = Resistor [tolerance=±5% resistance=220 package=THT]
  R21 = Resistor [tolerance=±5% resistance=220 package=THT]
  R22 = Resistor [tolerance=±5% resistance=220 package=THT]
  R23 = Resistor [tolerance=±5% resistance=220 package=THT]
  R24 = Resistor [tolerance=±5% resistance=220 package=THT]
  R25 = Resistor [tolerance=±5% resistance=220 package=THT]
  R26 = Resistor [tolerance=±5% resistance=220 package=THT]
  R27 = Resistor [tolerance=±5% resistance=220 package=THT]
  U5 = 74HC595 [package="DIP16 [THT]"]
  R28 = Resistor [tolerance=±5% resistance=220 package=THT]
  R29 = Resistor [tolerance=±5% resistance=220 package=THT]
  R30 = Resistor [tolerance=±5% resistance=220 package=THT]
  R31 = Resistor [tolerance=±5% resistance=220 package=THT]
  R32 = Resistor [tolerance=±5% resistance=220 package=THT]
  R33 = Resistor [tolerance=±5% resistance=220 package=THT]
  R34 = Resistor [tolerance=±5% resistance=220 package=THT]
  R35 = Resistor [tolerance=±5% resistance=220 package=THT]
  U6 = 74HC595 [package="DIP16 [THT]"]
  R36 = Resistor [tolerance=±5% resistance=220 package=THT]
  R37 = Resistor [tolerance=±5% resistance=220 package=THT]
  R38 = Resistor [tolerance=±5% resistance=220 package=THT]
  R39 = Resistor [tolerance=±5% resistance=220 package=THT]
  R40 = Resistor [tolerance=±5% resistance=220 package=THT]
  R41 = Resistor [tolerance=±5% resistance=220 package=THT]
  R42 = Resistor [tolerance=±5% resistance=220 package=THT]
  R43 = Resistor [tolerance=±5% resistance=220 package=THT]
  U7 = 74HC595 [package="DIP16 [THT]"]
  R44 = Resistor [tolerance=±5% resistance=220 package=THT]
  R45 = Resistor [tolerance=±5% resistance=220 package=THT]
  R46 = Resistor [tolerance=±5% resistance=220 package=THT]
  R47 = Resistor [tolerance=±5% resistance=220 package=THT]
  R48 = Resistor [tolerance=±5% resistance=220 package=THT]
  R49 = Resistor [tolerance=±5% resistance=220 package=THT]
  R50 = Resistor [tolerance=±5% resistance=220 package=THT]
  R51 = Resistor [tolerance=±5% resistance=220 package=THT]
  U8 = 74HC595 [package="DIP16 [THT]"]
  R52 = Resistor [tolerance=±5% resistance=220 package=THT]
  R53 = Resistor [tolerance=±5% resistance=220 package=THT]
  R54 = Resistor [tolerance=±5% resistance=220 package=THT]
  R55 = Resistor [tolerance=±5% resistance=220 package=THT]
  R56 = Resistor [tolerance=±5% resistance=220 package=THT]
  R57 = Resistor [tolerance=±5% resistance=220 package=THT]
  R58 = Resistor [tolerance=±5% resistance=220 package=THT]
  R59 = Resistor [tolerance=±5% resistance=220 package=THT]
  U9 = 74HC595 [package="DIP16 [THT]"]
  R60 = Resistor [tolerance=±5% resistance=220 package=THT]
  R61 = Resistor [tolerance=±5% resistance=220 package=THT]
  R62 = Resistor [tolerance=±5% resistance=220 package=THT]
  R63 = Resistor [tolerance=±5% resistance=220 package=THT]
  R64 = Resistor [tolerance=±5% resistance=220 package=THT]
  R65 = Resistor [tolerance=±5% resistance=220 package=THT]
  R66 = Resistor [tolerance=±5% resistance=220 package=THT]
  R67 = Resistor [tolerance=±5% resistance=220 package=THT]
  J1 = screw terminal, 2 pins
  Arduino_NANO = Arduino Nano (Rev3.0)
  D1 = Rectifier Diode [part_number=1N4001 package="300 mil [THT]"]
  LAYER1-8 = mystery part, 8 pins [chip_label=?]
  LED1-8 = mystery part, 8 pins [chip_label=?]
  LED9-16 = mystery part, 8 pins [chip_label=?]
  LED17-24 = mystery part, 8 pins [chip_label=?]
  LED_25-32 = mystery part, 8 pins [chip_label=?]
  LED_33-40 = mystery part, 8 pins [chip_label=?]
  LED_41-48 = mystery part, 8 pins [chip_label=?]
  LED_49-56 = mystery part, 8 pins [chip_label=?]
  LED_57_-_64 = mystery part, 8 pins [chip_label=?]
  10uF = Electrolytic Capacitor [capacitance=10µF voltage=10V package="200 mil [THT, electrolytic]"]

nets:
  N1: U1.Q1, ULN2803.I7
  N2: U1.Q2, ULN2803.I6
  N3: U1.Q3, ULN2803.I5
  N4: U1.Q4, ULN2803.I4
  N5: U1.Q5, ULN2803.I3
  N6: U1.Q6, ULN2803.I2
  N7: U1.Q7, ULN2803.I1
  GND: U1.GND, U2.GND, U3.GND, ULN2803.GND, U4.GND, U5.GND, U6.GND, U7.GND, U8.GND, U9.GND, J1.pin1, Arduino_NANO.GND, 10uF.-
  N8: U1.Q7', U3.DS
  VCC: U1.MR, U1.VCC, U2.MR, U2.VCC, U3.MR, U3.VCC, U4.MR, U4.VCC, U5.MR, U5.VCC, U6.MR, U6.VCC, U7.MR, U7.VCC, U8.MR, U8.VCC, U9.MR, U9.VCC, J1.pin2, D1.anode, 10uF.+
  N9: U1.SH_CP, U2.SH_CP, U3.SH_CP, U4.SH_CP, U5.SH_CP, U6.SH_CP, U7.SH_CP, U8.SH_CP, U9.SH_CP, Arduino_NANO.D13/SCK
  N10: U1.ST_CP, U2.ST_CP, U3.ST_CP, U4.ST_CP, U5.ST_CP, U6.ST_CP, U7.ST_CP, U8.ST_CP, U9.ST_CP, Arduino_NANO.D9
  N11: U1.OE, U2.OE, U3.OE, U4.OE, U5.OE, U6.OE, U7.OE, U8.OE, U9.OE, Arduino_NANO.D10
  N12: U1.DS, Arduino_NANO.D11/MOSI
  N13: U1.Q0, ULN2803.I8
  N14: U2.Q1, R12.Pin_0
  N15: U2.Q2, R11.Pin_0
  N16: U2.Q3, R10.Pin_0
  N17: U2.Q4, R9.Pin_0
  N18: U2.Q5, R8.Pin_0
  N19: U2.Q6, R7.Pin_0
  N20: U2.Q7, R6.Pin_0
  N21: U2.Q7', U4.DS
  N22: U2.DS, U3.Q7'
  N23: U2.Q0, R3.Pin_0
  N24: U3.Q1, R4.Pin_0
  N25: U3.Q2, R19.Pin_0
  N26: U3.Q3, R18.Pin_0
  N27: U3.Q4, R17.Pin_0
  N28: U3.Q5, R16.Pin_0
  N29: U3.Q6, R15.Pin_0
  N30: U3.Q7, R14.Pin_0
  N31: U3.Q0, R2.Pin_0
  N32: R2.Pin_1, LED1-8.pin1
  N33: R3.Pin_1, LED9-16.pin1
  N34: R4.Pin_1, LED1-8.pin2
  N35: R6.Pin_1, LED9-16.pin8
  N36: R7.Pin_1, LED9-16.pin7
  N37: R8.Pin_1, LED9-16.pin6
  N38: R9.Pin_1, LED9-16.pin5
  N39: R10.Pin_1, LED9-16.pin4
  N40: R11.Pin_1, LED9-16.pin3
  N41: R12.Pin_1, LED9-16.pin2
  N42: R14.Pin_1, LED1-8.pin8
  N43: R15.Pin_1, LED1-8.pin7
  N44: R16.Pin_1, LED1-8.pin6
  N45: R17.Pin_1, LED1-8.pin5
  N46: R18.Pin_1, LED1-8.pin4
  N47: R19.Pin_1, LED1-8.pin3
  N48: ULN2803.COMMON, Arduino_NANO.5V, D1.cathode
  N49: ULN2803.O8, LAYER1-8.pin1
  N50: ULN2803.O7, LAYER1-8.pin2
  N51: ULN2803.O6, LAYER1-8.pin3
  N52: ULN2803.O5, LAYER1-8.pin4
  N53: ULN2803.O4, LAYER1-8.pin5
  N54: ULN2803.O3, LAYER1-8.pin6
  N55: ULN2803.O2, LAYER1-8.pin7
  N56: ULN2803.O1, LAYER1-8.pin8
  N57: U4.Q1, R20.Pin_0
  N58: U4.Q2, R21.Pin_0
  N59: U4.Q3, R22.Pin_0
  N60: U4.Q4, R23.Pin_0
  N61: U4.Q5, R24.Pin_0
  N62: U4.Q6, R25.Pin_0
  N63: U4.Q7, R26.Pin_0
  N64: U4.Q7', U5.DS
  N65: U4.Q0, R27.Pin_0
  N66: R20.Pin_1, LED17-24.pin2
  N67: R21.Pin_1, LED17-24.pin3
  N68: R22.Pin_1, LED17-24.pin4
  N69: R23.Pin_1, LED17-24.pin5
  N70: R24.Pin_1, LED17-24.pin6
  N71: R25.Pin_1, LED17-24.pin7
  N72: R26.Pin_1, LED17-24.pin8
  N73: R27.Pin_1, LED17-24.pin1
  N74: U5.Q1, R28.Pin_0
  N75: U5.Q2, R29.Pin_0
  N76: U5.Q3, R30.Pin_0
  N77: U5.Q4, R31.Pin_0
  N78: U5.Q5, R32.Pin_0
  N79: U5.Q6, R33.Pin_0
  N80: U5.Q7, R34.Pin_0
  N81: U5.Q7', U6.DS
  N82: U5.Q0, R35.Pin_0
  N83: R28.Pin_1, LED_25-32.pin7
  N84: R29.Pin_1, LED_25-32.pin6
  N85: R30.Pin_1, LED_25-32.pin5
  N86: R31.Pin_1, LED_25-32.pin4
  N87: R32.Pin_1, LED_25-32.pin3
  N88: R33.Pin_1, LED_25-32.pin2
  N89: R34.Pin_1, LED_25-32.pin1
  N90: R35.Pin_1, LED_25-32.pin8
  N91: U6.Q1, R36.Pin_0
  N92: U6.Q2, R37.Pin_0
  N93: U6.Q3, R38.Pin_0
  N94: U6.Q4, R39.Pin_0
  N95: U6.Q5, R40.Pin_0
  N96: U6.Q6, R41.Pin_0
  N97: U6.Q7, R42.Pin_0
  N98: U6.Q7', U7.DS
  N99: U6.Q0, R43.Pin_0
  N100: R36.Pin_1, LED_33-40.pin7
  N101: R37.Pin_1, LED_33-40.pin6
  N102: R38.Pin_1, LED_33-40.pin5
  N103: R39.Pin_1, LED_33-40.pin4
  N104: R40.Pin_1, LED_33-40.pin3
  N105: R41.Pin_1, LED_33-40.pin2
  N106: R42.Pin_1, LED_33-40.pin1
  N107: R43.Pin_1, LED_33-40.pin8
  N108: U7.Q1, R44.Pin_0
  N109: U7.Q2, R45.Pin_0
  N110: U7.Q3, R46.Pin_0
  N111: U7.Q4, R47.Pin_0
  N112: U7.Q5, R48.Pin_0
  N113: U7.Q6, R49.Pin_0
  N114: U7.Q7, R50.Pin_0
  N115: U7.Q7', U8.DS
  N116: U7.Q0, R51.Pin_0
  N117: R44.Pin_1, LED_41-48.pin7
  N118: R45.Pin_1, LED_41-48.pin6
  N119: R46.Pin_1, LED_41-48.pin5
  N120: R47.Pin_1, LED_41-48.pin4
  N121: R48.Pin_1, LED_41-48.pin3
  N122: R49.Pin_1, LED_41-48.pin2
  N123: R50.Pin_1, LED_41-48.pin1
  N124: R51.Pin_1, LED_41-48.pin8
  N125: U8.Q1, R52.Pin_0
  N126: U8.Q2, R53.Pin_0
  N127: U8.Q3, R54.Pin_0
  N128: U8.Q4, R55.Pin_0
  N129: U8.Q5, R56.Pin_0
  N130: U8.Q6, R57.Pin_0
  N131: U8.Q7, R58.Pin_0
  N132: U8.Q7', U9.DS
  N133: U8.Q0, R59.Pin_0
  N134: R52.Pin_1, LED_49-56.pin7
  N135: R53.Pin_1, LED_49-56.pin6
  N136: R54.Pin_1, LED_49-56.pin5
  N137: R55.Pin_1, LED_49-56.pin4
  N138: R56.Pin_1, LED_49-56.pin3
  N139: R57.Pin_1, LED_49-56.pin2
  N140: R58.Pin_1, LED_49-56.pin1
  N141: R59.Pin_1, LED_49-56.pin8
  N142: U9.Q1, R60.Pin_0
  N143: U9.Q2, R61.Pin_0
  N144: U9.Q3, R62.Pin_0
  N145: U9.Q4, R63.Pin_0
  N146: U9.Q5, R64.Pin_0
  N147: U9.Q6, R65.Pin_0
  N148: U9.Q7, R66.Pin_0
  N149: U9.Q0, R67.Pin_0
  N150: R60.Pin_1, LED_57_-_64.pin7
  N151: R61.Pin_1, LED_57_-_64.pin6
  N152: R62.Pin_1, LED_57_-_64.pin5
  N153: R63.Pin_1, LED_57_-_64.pin4
  N154: R64.Pin_1, LED_57_-_64.pin3
  N155: R65.Pin_1, LED_57_-_64.pin2
  N156: R66.Pin_1, LED_57_-_64.pin1
  N157: R67.Pin_1, LED_57_-_64.pin8

notes:
  -
  5V
  +++ 5V +++
  GND
  C
  C1
  USB
  74HC595
  ULN2803
  R1-R64 330-500
  C - 100nF
  SINGLE COLOR 8x8x8 LED CUBE V2
  OUT
  LATCH
  /OE
  CLOCK
  VCC
  Bakisha2018

custom parts:
  ULN2803 Darlington Array: ULN2803 Darlington Transistor Array with Flyback Protection
