# Fritzing sketch Bluepill_4x4x4_RGB_595_BLUEPILL_V1_build004 (saved by Fritzing 0.9.3b)
circuit board: 15cm x 10cm
breadboards: 1

parts:
  ULN2803-4 = ULN2803A [package=THT]
  U7 = 74HC595 [package="DIP16 [THT]"]
  R44 = Resistor [tolerance=±5% resistance=220 package=THT]
  R45 = Resistor [tolerance=±5% resistance=220 package=THT]
  R46 = Resistor [tolerance=±5% resistance=220 package=THT]
  R47 = Resistor [tolerance=±5% resistance=220 package=THT]
  R48 = Resistor [tolerance=±5% resistance=220 package=THT]
  R49 = Resistor [tolerance=±5% resistance=220 package=THT]
  R50 = Resistor [tolerance=±5% resistance=220 package=THT]
  R51 = Resistor [tolerance=±5% resistance=220 package=THT]
  ULN2803-5 = ULN2803A [package=THT]
  U8 = 74HC595 [package="DIP16 [THT]"]
  R52 = Resistor [tolerance=±5% resistance=220 package=THT]
  R53 = Resistor [tolerance=±5% resistance=220 package=THT]
  R54 = Resistor [tolerance=±5% resistance=220 package=THT]
  R55 = Resistor [tolerance=±5% resistance=220 package=THT]
  R56 = Resistor [tolerance=±5% resistance=220 package=THT]
  R57 = Resistor [tolerance=±5% resistance=220 package=THT]
  R58 = Resistor [tolerance=±5% resistance=220 package=THT]
  R59 = Resistor [tolerance=±5% resistance=220 package=THT]
  ULN2803-6 = ULN2803A [package=THT]
  U9 = 74HC595 [package="DIP16 [THT]"]
  R60 = Resistor [tolerance=±5% resistance=220 package=THT]
  R61 = Resistor [tolerance=±5% resistance=220 package=THT]
  R62 = Resistor [tolerance=±5% resistance=220 package=THT]
  R63 = Resistor [tolerance=±5% resistance=220 package=THT]
  R64 = Resistor [tolerance=±5% resistance=220 package=THT]
  R65 = Resistor [tolerance=±5% resistance=220 package=THT]
  R66 = Resistor [tolerance=±5% resistance=220 package=THT]
  R67 = Resistor [tolerance=±5% resistance=220 package=THT]
  ULN2803-3 = ULN2803A [package=THT]
  U11 = 74HC595 [package="DIP16 [THT]"]
  R76 = Resistor [tolerance=±5% resistance=220 package=THT]
  R77 = Resistor [tolerance=±5% resistance=220 package=THT]
  R78 = Resistor [tolerance=±5% resistance=220 package=THT]
  R79 = Resistor [tolerance=±5% resistance=220 package=THT]
  R80 = Resistor [tolerance=±5% resistance=220 package=THT]
  R81 = Resistor [tolerance=±5% resistance=220 package=THT]
  R82 = Resistor [tolerance=±5% resistance=220 package=THT]
  R83 = Resistor [tolerance=±5% resistance=220 package=THT]
  ULN2803-2 = ULN2803A [package=THT]
  U12 = 74HC595 [package="DIP16 [THT]"]
  R84 = Resistor [tolerance=±5% resistance=220 package=THT]
  R85 = Resistor [tolerance=±5% resistance=220 package=THT]
  R86 = Resistor [tolerance=±5% resistance=220 package=THT]
  R87 = Resistor [tolerance=±5% resistance=220 package=THT]
  R88 = Resistor [tolerance=±5% resistance=220 package=THT]
  R89 = Resistor [tolerance=±5% resistance=220 package=THT]
  R90 = Resistor [tolerance=±5% resistance=220 package=THT]
  R91 = Resistor [tolerance=±5% resistance=220 package=THT]
  ULN2803-1 = ULN2803A [package=THT]
  U13 = 74HC595 [package="DIP16 [THT]"]
  R92 = Resistor [tolerance=±5% resistance=220 package=THT]
  R93 = Resistor [tolerance=±5% resistance=220 package=THT]
  R94 = Resistor [tolerance=±5% resistance=220 package=THT]
  R95 = Resistor [tolerance=±5% resistance=220 package=THT]
  R96 = Resistor [tolerance=±5% resistance=220 package=THT]
  R97 = Resistor [tolerance=±5% resistance=220 package=THT]
  R98 = Resistor [tolerance=±5% resistance=220 package=THT]
  R99 = Resistor [tolerance=±5% resistance=220 package=THT]
  U14 = 74HC595 [package="DIP16 [THT]"]
  R100 = Resistor [tolerance=±5% resistance=220 package=THT]
  R101 = Resistor [tolerance=±5% resistance=220 package=THT]
  R106 = Resistor [tolerance=±5% resistance=220 package=THT]
  R107 = Resistor [tolerance=±5% resistance=220 package=THT]
  LED2B = mystery part, 8 pins [chip_label=?]
  LED1R = mystery part, 8 pins [chip_label=?]
  LED2G = mystery part, 8 pins [chip_label=?]
  LED1G = mystery part, 8 pins [chip_label=?]
  LED1B = mystery part, 8 pins [chip_label=?]
  LED2R = mystery part, 8 pins [chip_label=?]
  ULN2003 = ULN2003A [package="DIP16 [THT]"]
  1K-Pullup = mystery part, 9 pins [chip_label=?]
  Q1 = PNP-Transistor [package="TO92 [THT]"]
  J1 = screw terminal, 2 pins
  J2 = screw terminal, 2 pins
  Q2 = PNP-Transistor [package="TO92 [THT]"]
  Q3 = PNP-Transistor [package="TO92 [THT]"]
  Q4 = PNP-Transistor [package="TO92 [THT]"]
  C1 = Electrolytic Capacitor [capacitance=1µF package="100 mil [THT, electrolytic]"]
  C2 = Electrolytic Capacitor [capacitance=1µF package="100 mil [THT, electrolytic]"]
  BluePill = IC, DIP package, 40 pins [chip_label=IC]

nets:
  N1: ULN2803-4.In_1, U7.Q7
  N2: ULN2803-4.In_2, U7.Q6
  N3: ULN2803-4.In_3, U7.Q5
  N4: ULN2803-4.In_4, U7.Q4
  N5: ULN2803-4.In_5, U7.Q3
  N6: ULN2803-4.In_6, U7.Q2
  N7: ULN2803-4.In_7, U7.Q1
  N8: ULN2803-4.In_8, U7.Q0
  N9: ULN2803-4.0V, ULN2803-5.0V, ULN2803-6.0V, ULN2803-3.0V, ULN2803-2.0V, ULN2803-1.0V, ULN2003.0V, C1.-, BluePill.pin19
  N10: ULN2803-4.Out_8, R51.Pin_0
  N11: ULN2803-4.Out_7, R44.Pin_0
  N12: ULN2803-4.Out_6, R45.Pin_0
  N13: ULN2803-4.Out_5, R46.Pin_0
  N14: ULN2803-4.Out_4, R47.Pin_0
  N15: ULN2803-4.Out_3, R48.Pin_0
  N16: ULN2803-4.Out_2, R49.Pin_0
  N17: ULN2803-4.Out_1, R50.Pin_0
  GND: U7.GND, U8.GND, U9.GND, U11.GND, U12.GND, U13.GND, U14.GND, C2.-
  N18: U7.Q7', U8.DS
  VCC: U7.MR, U7.VCC, U8.MR, U8.VCC, U9.MR, U9.VCC, U11.MR, U11.VCC, U12.MR, U12.VCC, U13.MR, U13.VCC, U14.MR, U14.VCC, C2.+, BluePill.pin20
  N19: U7.SH_CP, U8.SH_CP, U9.SH_CP, U11.SH_CP, U12.SH_CP, U13.SH_CP
  N20: U7.ST_CP, U8.ST_CP, U9.ST_CP, U11.ST_CP, U12.ST_CP, U13.ST_CP, U14.ST_CP, BluePill.pin26
  N21: U7.OE, U8.OE, U9.OE, U11.OE, U12.OE, U13.OE, U14.OE, BluePill.pin25
  N22: U7.DS, U11.Q7'
  N23: R44.Pin_1, LED2G.pin2
  N24: R45.Pin_1, LED2G.pin3
  N25: R46.Pin_1, LED2G.pin4
  N26: R47.Pin_1, LED2G.pin5
  N27: R48.Pin_1, LED2G.pin6
  N28: R49.Pin_1, LED2G.pin7
  N29: R50.Pin_1, LED2G.pin8
  N30: R51.Pin_1, LED2G.pin1
  N31: ULN2803-5.In_1, U8.Q7
  N32: ULN2803-5.In_2, U8.Q6
  N33: ULN2803-5.In_3, U8.Q5
  N34: ULN2803-5.In_4, U8.Q4
  N35: ULN2803-5.In_5, U8.Q3
  N36: ULN2803-5.In_6, U8.Q2
  N37: ULN2803-5.In_7, U8.Q1
  N38: ULN2803-5.In_8, U8.Q0
  N39: ULN2803-5.Out_8, R59.Pin_0
  N40: ULN2803-5.Out_7, R52.Pin_0
  N41: ULN2803-5.Out_6, R53.Pin_0
  N42: ULN2803-5.Out_5, R54.Pin_0
  N43: ULN2803-5.Out_4, R55.Pin_0
  N44: ULN2803-5.Out_3, R56.Pin_0
  N45: ULN2803-5.Out_2, R57.Pin_0
  N46: ULN2803-5.Out_1, R58.Pin_0
  N47: U8.Q7', U9.DS
  N48: R52.Pin_1, LED1B.pin2
  N49: R53.Pin_1, LED1B.pin3
  N50: R54.Pin_1, LED1B.pin4
  N51: R55.Pin_1, LED1B.pin5
  N52: R56.Pin_1, LED1B.pin6
  N53: R57.Pin_1, LED1B.pin7
  N54: R58.Pin_1, LED1B.pin8
  N55: R59.Pin_1, LED1B.pin1
  N56: ULN2803-6.In_1, U9.Q7
  N57: ULN2803-6.In_2, U9.Q6
  N58: ULN2803-6.In_3, U9.Q5
  N59: ULN2803-6.In_4, U9.Q4
  N60: ULN2803-6.In_5, U9.Q3
  N61: ULN2803-6.In_6, U9.Q2
  N62: ULN2803-6.In_7, U9.Q1
  N63: ULN2803-6.In_8, U9.Q0
  N64: ULN2803-6.Out_8, R67.Pin_0
  N65: ULN2803-6.Out_7, R60.Pin_0
  N66: ULN2803-6.Out_6, R61.Pin_0
  N67: ULN2803-6.Out_5, R62.Pin_0
  N68: ULN2803-6.Out_4, R63.Pin_0
  N69: ULN2803-6.Out_3, R64.Pin_0
  N70: ULN2803-6.Out_2, R65.Pin_0
  N71: ULN2803-6.Out_1, R66.Pin_0
  N72: R60.Pin_1, LED2B.pin2
  N73: R61.Pin_1, LED2B.pin3
  N74: R62.Pin_1, LED2B.pin4
  N75: R63.Pin_1, LED2B.pin5
  N76: R64.Pin_1, LED2B.pin6
  N77: R65.Pin_1, LED2B.pin7
  N78: R66.Pin_1, LED2B.pin8
  N79: R67.Pin_1, LED2B.pin1
  N80: ULN2803-3.In_1, U11.Q7
  N81: ULN2803-3.In_2, U11.Q6
  N82: ULN2803-3.In_3, U11.Q5
  N83: ULN2803-3.In_4, U11.Q4
  N84: ULN2803-3.In_5, U11.Q3
  N85: ULN2803-3.In_6, U11.Q2
  N86: ULN2803-3.In_7, U11.Q1
  N87: ULN2803-3.In_8, U11.Q0
  N88: ULN2803-3.Out_8, R83.Pin_0
  N89: ULN2803-3.Out_7, R82.Pin_0
  N90: ULN2803-3.Out_6, R76.Pin_0
  N91: ULN2803-3.Out_5, R77.Pin_0
  N92: ULN2803-3.Out_4, R78.Pin_0
  N93: ULN2803-3.Out_3, R79.Pin_0
  N94: ULN2803-3.Out_2, R80.Pin_0
  N95: ULN2803-3.Out_1, R81.Pin_0
  N96: U11.DS, U12.Q7'
  N97: R76.Pin_1, LED1G.pin6
  N98: R77.Pin_1, LED1G.pin5
  N99: R78.Pin_1, LED1G.pin4
  N100: R79.Pin_1, LED1G.pin3
  N101: R80.Pin_1, LED1G.pin2
  N102: R81.Pin_1, LED1G.pin1
  N103: R82.Pin_1, LED1G.pin7
  N104: R83.Pin_1, LED1G.pin8
  N105: ULN2803-2.In_1, U12.Q7
  N106: ULN2803-2.In_2, U12.Q6
  N107: ULN2803-2.In_3, U12.Q5
  N108: ULN2803-2.In_4, U12.Q4
  N109: ULN2803-2.In_5, U12.Q3
  N110: ULN2803-2.In_6, U12.Q2
  N111: ULN2803-2.In_7, U12.Q1
  N112: ULN2803-2.In_8, U12.Q0
  N113: ULN2803-2.Out_8, R91.Pin_0
  N114: ULN2803-2.Out_7, R90.Pin_0
  N115: ULN2803-2.Out_6, R84.Pin_0
  N116: ULN2803-2.Out_5, R85.Pin_0
  N117: ULN2803-2.Out_4, R86.Pin_0
  N118: ULN2803-2.Out_3, R87.Pin_0
  N119: ULN2803-2.Out_2, R88.Pin_0
  N120: ULN2803-2.Out_1, R89.Pin_0
  N121: U12.DS, U13.Q7'
  N122: R84.Pin_1, LED2R.pin6
  N123: R85.Pin_1, LED2R.pin5
  N124: R86.Pin_1, LED2R.pin4
  N125: R87.Pin_1, LED2R.pin3
  N126: R88.Pin_1, LED2R.pin2
  N127: R89.Pin_1, LED2R.pin1
  N128: R90.Pin_1, LED2R.pin7
  N129: R91.Pin_1, LED2R.pin8
  N130: ULN2803-1.In_1, U13.Q7
  N131: ULN2803-1.In_2, U13.Q6
  N132: ULN2803-1.In_3, U13.Q5
  N133: ULN2803-1.In_4, U13.Q4
  N134: ULN2803-1.In_5, U13.Q3
  N135: ULN2803-1.In_6, U13.Q2
  N136: ULN2803-1.In_7, U13.Q1
  N137: ULN2803-1.In_8, U13.Q0
  N138: ULN2803-1.Out_8, R99.Pin_0
  N139: ULN2803-1.Out_7, R98.Pin_0
  N140: ULN2803-1.Out_6, R92.Pin_0
  N141: ULN2803-1.Out_5, R93.Pin_0
  N142: ULN2803-1.Out_4, R94.Pin_0
  N143: ULN2803-1.Out_3, R95.Pin_0
  N144: ULN2803-1.Out_2, R96.Pin_0
  N145: ULN2803-1.Out_1, R97.Pin_0
  N146: U13.DS, U14.Q7'
  N147: R92.Pin_1, LED1R.pin6
  N148: R93.Pin_1, LED1R.pin5
  N149: R94.Pin_1, LED1R.pin4
  N150: R95.Pin_1, LED1R.pin3
  N151: R96.Pin_1, LED1R.pin2
  N152: R97.Pin_1, LED1R.pin1
  N153: R98.Pin_1, LED1R.pin7
  N154: R99.Pin_1, LED1R.pin8
  N155: U14.Q1, ULN2003.In_6
  N156: U14.Q2, ULN2003.In_5
  N157: U14.Q3, ULN2003.In_4
  N158: U14.SH_CP, BluePill.pin30
  N159: U14.DS, BluePill.pin32
  N160: U14.Q0, ULN2003.In_7
  N161: R100.Pin_0, ULN2003.Out_5, 1K-Pullup.pin4
  N162: R100.Pin_1, Q3.B
  N163: R101.Pin_0, ULN2003.Out_4, 1K-Pullup.pin5
  N164: R101.Pin_1, Q4.B
  N165: R106.Pin_0, ULN2003.Out_6, 1K-Pullup.pin3
  N166: R106.Pin_1, Q2.B
  N167: R107.Pin_0, ULN2003.Out_7, 1K-Pullup.pin2
  N168: R107.Pin_1, Q1.B
  N169: 1K-Pullup.pin1, Q1.E, Q2.E, Q3.E, Q4.E, C1.+, BluePill.pin18
  N170: Q1.C, J2.pin2
  N171: J1.pin1, Q4.C
  N172: J1.pin2, Q3.C
  N173: J2.pin1, Q2.C

notes:
  VCC
  CLOCK
  /OE
  LATCH
  GND
  OUT
  VCC 5V
  Power GND
  Bakisha2018
  74HC595
  C
  DATA_OUT
  100
  LAYER
  4 3  2  1
  USB
  PA1 - LE
  PA0 - OE/
  PA7 -MOSI
  PA5 -CLK
