# Fritzing sketch 4x4x4_RGB_CUBE_BLUEPILL-led_layer (saved by Fritzing 0.9.3b)
circuit board: 10cm x 10cm
breadboards: 1

parts:
  B> = mystery part, 4 pins [chip_label=?]
  <-RED6 = mystery part, 4 pins [chip_label=?]
  <-RED7 = mystery part, 4 pins [chip_label=?]
  <R = mystery part, 4 pins [chip_label=?]
  <-RED4 = mystery part, 4 pins [chip_label=?]
  <G = mystery part, 4 pins [chip_label=?]
  <-G1 = mystery part, 4 pins [chip_label=?]
  <-RED8 = mystery part, 4 pins [chip_label=?]
  <G1 = mystery part, 4 pins [chip_label=?]
  <-G2 = mystery part, 4 pins [chip_label=?]
  <R_2 = mystery part, 4 pins [chip_label=?]
  <-RED5 = mystery part, 4 pins [chip_label=?]
  1-2-3-4_Layer = mystery part, 4 pins [chip_label=?]
  B>17 = mystery part, 1 pin [chip_label=?]
  B>18 = mystery part, 1 pin [chip_label=?]
  B>19 = mystery part, 1 pin [chip_label=?]
  B>20 = mystery part, 1 pin [chip_label=?]
  B>21 = mystery part, 1 pin [chip_label=?]
  B>22 = mystery part, 1 pin [chip_label=?]
  B>23 = mystery part, 1 pin [chip_label=?]
  B>24 = mystery part, 1 pin [chip_label=?]
  B>25 = mystery part, 1 pin [chip_label=?]
  B>26 = mystery part, 1 pin [chip_label=?]
  B>27 = mystery part, 1 pin [chip_label=?]
  B>28 = mystery part, 1 pin [chip_label=?]
  B>29 = mystery part, 1 pin [chip_label=?]
  B>30 = mystery part, 1 pin [chip_label=?]
  B>31 = mystery part, 1 pin [chip_label=?]
  B>32 = mystery part, 1 pin [chip_label=?]
  B>33 = mystery part, 1 pin [chip_label=?]
  B>34 = mystery part, 1 pin [chip_label=?]
  B>35 = mystery part, 1 pin [chip_label=?]
  B>36 = mystery part, 1 pin [chip_label=?]
  B>37 = mystery part, 1 pin [chip_label=?]
  B>38 = mystery part, 1 pin [chip_label=?]
  B>39 = mystery part, 1 pin [chip_label=?]
  B>40 = mystery part, 1 pin [chip_label=?]
  B>41 = mystery part, 1 pin [chip_label=?]
  B>42 = mystery part, 1 pin [chip_label=?]
  B>43 = mystery part, 1 pin [chip_label=?]
  B>44 = mystery part, 1 pin [chip_label=?]
  B>45 = mystery part, 1 pin [chip_label=?]
  B>46 = mystery part, 1 pin [chip_label=?]
  B>47 = mystery part, 1 pin [chip_label=?]
  B>48 = mystery part, 1 pin [chip_label=?]
  B>49 = mystery part, 1 pin [chip_label=?]
  B>50 = mystery part, 1 pin [chip_label=?]
  B>51 = mystery part, 1 pin [chip_label=?]
  B>52 = mystery part, 1 pin [chip_label=?]
  B>53 = mystery part, 1 pin [chip_label=?]
  B>54 = mystery part, 1 pin [chip_label=?]
  B>55 = mystery part, 1 pin [chip_label=?]
  B>56 = mystery part, 1 pin [chip_label=?]
  B>57 = mystery part, 1 pin [chip_label=?]
  B>58 = mystery part, 1 pin [chip_label=?]
  B>59 = mystery part, 1 pin [chip_label=?]
  B>60 = mystery part, 1 pin [chip_label=?]
  B>61 = mystery part, 1 pin [chip_label=?]
  B>62 = mystery part, 1 pin [chip_label=?]
  B>63 = mystery part, 1 pin [chip_label=?]
  B>64 = mystery part, 1 pin [chip_label=?]
  B>65 = mystery part, 1 pin [chip_label=?]
  B>66 = mystery part, 1 pin [chip_label=?]
  B>67 = mystery part, 1 pin [chip_label=?]
  B>68 = mystery part, 1 pin [chip_label=?]

nets:
  N1: B>.pin1, B>31.pin1
  N2: B>.pin2, B>28.pin1
  N3: B>.pin3, B>25.pin1
  N4: B>.pin4, B>22.pin1
  N5: <-RED6.pin1, B>34.pin1
  N6: <-RED6.pin2, B>37.pin1
  N7: <-RED6.pin3, B>40.pin1
  N8: <-RED6.pin4, B>43.pin1
  N9: <-RED7.pin1, B>46.pin1
  N10: <-RED7.pin2, B>49.pin1
  N11: <-RED7.pin3, B>52.pin1
  N12: <-RED7.pin4, B>55.pin1
  N13: <R.pin1, B>29.pin1
  N14: <R.pin2, B>26.pin1
  N15: <R.pin3, B>23.pin1
  N16: <R.pin4, B>20.pin1
  N17: <-RED4.pin1, B>32.pin1
  N18: <-RED4.pin2, B>35.pin1
  N19: <-RED4.pin3, B>38.pin1
  N20: <-RED4.pin4, B>41.pin1
  N21: <G.pin1, B>21.pin1
  N22: <G.pin2, B>24.pin1
  N23: <G.pin3, B>27.pin1
  N24: <G.pin4, B>30.pin1
  N25: <-G1.pin1, B>42.pin1
  N26: <-G1.pin2, B>39.pin1
  N27: <-G1.pin3, B>36.pin1
  N28: <-G1.pin4, B>33.pin1
  N29: <-RED8.pin1, B>19.pin1
  N30: <-RED8.pin2, B>58.pin1
  N31: <-RED8.pin3, B>61.pin1
  N32: <-RED8.pin4, B>64.pin1
  N33: <G1.pin1, B>54.pin1
  N34: <G1.pin2, B>51.pin1
  N35: <G1.pin3, B>48.pin1
  N36: <G1.pin4, B>45.pin1
  N37: <-G2.pin1, B>63.pin1
  N38: <-G2.pin2, B>60.pin1
  N39: <-G2.pin3, B>57.pin1
  N40: <-G2.pin4, B>18.pin1
  N41: <R_2.pin1, B>44.pin1
  N42: <R_2.pin2, B>47.pin1
  N43: <R_2.pin3, B>50.pin1
  N44: <R_2.pin4, B>53.pin1
  N45: <-RED5.pin1, B>17.pin1
  N46: <-RED5.pin2, B>56.pin1
  N47: <-RED5.pin3, B>59.pin1
  N48: <-RED5.pin4, B>62.pin1
  N49: 1-2-3-4_Layer.pin1, B>65.pin1
  N50: 1-2-3-4_Layer.pin2, B>66.pin1
  N51: 1-2-3-4_Layer.pin3, B>67.pin1
  N52: 1-2-3-4_Layer.pin4, B>68.pin1

notes:
  VCC
  CLOCK
  /OE
  LATCH
  GND
  OUT
  Bakisha2018
  74HC595
  C
  VCC 5V
  USB
  16x
  PA0 - OE/
  4x4x4 BLUEPILL  RGB CUBE
  LED-3-3
  LED-0-0
  LED-0-1
  LED-0-2
  LED-0-3
  LED-1-3
  LED-1-2
  LED-1-1
  LED-1-0
  LED-2-3
  LED-2-2
  LED-2-1
  LED-2-0
  LED-3-2
  LED-3-1
  LED-3-0
  Design - BAKISHA 2019
