# Fritzing sketch 4x4x8_RGB_CUBE_BLUEPILL_V2 (saved by Fritzing 0.9.3b)
circuit board: 10cm x 10cm
breadboards: 1

parts:
  BLUEPILL = STM32F103C8T6 blue mini board
  UDN2981 = DIP - 18 pins [package="DIP (Dual Inline) [THT]"]
  74HC595-L = 74HC595 [package="DIP16 [THT]"]
  ULN2803-3 = ULN2803A [package=THT]
  G0-0 = Resistor [tolerance=±5% resistance=330 package=THT]
  74HC595-3 = 74HC595 [package="DIP16 [THT]"]
  C5 = Ceramic Capacitor [capacitance=100nF package="100 mil [THT, multilayer]"]
  ULN2803-4 = ULN2803A [package=THT]
  74HC595-4 = 74HC595 [package="DIP16 [THT]"]
  C6 = Ceramic Capacitor [capacitance=100nF package="100 mil [THT, multilayer]"]
  ULN2803-5 = ULN2803A [package=THT]
  74HC595-5 = 74HC595 [package="DIP16 [THT]"]
  C7 = Ceramic Capacitor [capacitance=100nF package="100 mil [THT, multilayer]"]
  ULN2803-6 = ULN2803A [package=THT]
  74HC595-6 = 74HC595 [package="DIP16 [THT]"]
  C3 = Ceramic Capacitor [capacitance=100nF package="100 mil [THT, multilayer]"]
  ULN2803-1 = ULN2803A [package=THT]
  R0-0 = Resistor [tolerance=±5% resistance=470 package=THT]
  74HC595-1 = 74HC595 [package="DIP16 [THT]"]
  C4 = Ceramic Capacitor [capacitance=100nF package="100 mil [THT, multilayer]"]
  ULN2803-2 = ULN2803A [package=THT]
  74HC595-2 = 74HC595 [package="DIP16 [THT]"]
  C2 = Ceramic Capacitor [capacitance=100nF package="100 mil [THT, multilayer]"]
  R0-1 = Resistor [tolerance=±5% resistance=470 package=THT]
  R0-2 = Resistor [tolerance=±5% resistance=470 package=THT]
  R0-3 = Resistor [tolerance=±5% resistance=470 package=THT]
  R1-0 = Resistor [tolerance=±5% resistance=470 package=THT]
  R1-1 = Resistor [tolerance=±5% resistance=470 package=THT]
  R1-2 = Resistor [tolerance=±5% resistance=470 package=THT]
  R1-3 = Resistor [tolerance=±5% resistance=470 package=THT]
  <RED = mystery part, 4 pins [chip_label=?]
  <-RED4 = mystery part, 4 pins [chip_label=?]
  <R = mystery part, 4 pins [chip_label=?]
  <-RED5 = mystery part, 4 pins [chip_label=?]
  R2-0 = Resistor [tolerance=±5% resistance=470 package=THT]
  R3-0 = Resistor [tolerance=±5% resistance=470 package=THT]
  R3-3 = Resistor [tolerance=±5% resistance=470 package=THT]
  R3-2 = Resistor [tolerance=±5% resistance=470 package=THT]
  R2-2 = Resistor [tolerance=±5% resistance=470 package=THT]
  R3-1 = Resistor [tolerance=±5% resistance=470 package=THT]
  R2-3 = Resistor [tolerance=±5% resistance=470 package=THT]
  R2-1 = Resistor [tolerance=±5% resistance=470 package=THT]
  G0-1 = Resistor [tolerance=±5% resistance=330 package=THT]
  G0-2 = Resistor [tolerance=±5% resistance=330 package=THT]
  G0-3 = Resistor [tolerance=±5% resistance=330 package=THT]
  G1-0 = Resistor [tolerance=±5% resistance=330 package=THT]
  G1-1 = Resistor [tolerance=±5% resistance=330 package=THT]
  G1-2 = Resistor [tolerance=±5% resistance=330 package=THT]
  G1-3 = Resistor [tolerance=±5% resistance=330 package=THT]
  G2-0 = Resistor [tolerance=±5% resistance=330 package=THT]
  G3-1 = Resistor [tolerance=±5% resistance=330 package=THT]
  G2-2 = Resistor [tolerance=±5% resistance=330 package=THT]
  G2-3 = Resistor [tolerance=±5% resistance=330 package=THT]
  G3-0 = Resistor [tolerance=±5% resistance=330 package=THT]
  G3-2 = Resistor [tolerance=±5% resistance=330 package=THT]
  G2-1 = Resistor [tolerance=±5% resistance=330 package=THT]
  G3-3 = Resistor [tolerance=±5% resistance=330 package=THT]
  <G = mystery part, 4 pins [chip_label=?]
  <-G1 = mystery part, 4 pins [chip_label=?]
  <-G2 = mystery part, 4 pins [chip_label=?]
  <G1 = mystery part, 4 pins [chip_label=?]
  BLUE> = mystery part, 4 pins [chip_label=?]
  <-RED6 = mystery part, 4 pins [chip_label=?]
  B0-0 = Resistor [tolerance=±5% resistance=330 package=THT]
  B0-1 = Resistor [tolerance=±5% resistance=330 package=THT]
  B0-2 = Resistor [tolerance=±5% resistance=330 package=THT]
  B0-3 = Resistor [tolerance=±5% resistance=330 package=THT]
  B1-0 = Resistor [tolerance=±5% resistance=330 package=THT]
  B1-1 = Resistor [tolerance=±5% resistance=330 package=THT]
  B1-2 = Resistor [tolerance=±5% resistance=330 package=THT]
  B1-3 = Resistor [tolerance=±5% resistance=330 package=THT]
  B2-2 = Resistor [tolerance=±5% resistance=330 package=THT]
  B3-3 = Resistor [tolerance=±5% resistance=330 package=THT]
  B3-1 = Resistor [tolerance=±5% resistance=330 package=THT]
  B2-3 = Resistor [tolerance=±5% resistance=330 package=THT]
  B3-1_2 = Resistor [tolerance=±5% resistance=330 package=THT]
  B2-0 = Resistor [tolerance=±5% resistance=330 package=THT]
  B2-1 = Resistor [tolerance=±5% resistance=330 package=THT]
  B3-2 = Resistor [tolerance=±5% resistance=330 package=THT]
  <-RED7 = mystery part, 4 pins [chip_label=?]
  <-RED8 = mystery part, 4 pins [chip_label=?]
  C9 = Electrolytic Capacitor [capacitance=10µF voltage=10V package="100 mil [THT, electrolytic]"]
  C8 = Ceramic Capacitor [capacitance=100nF package="100 mil [THT, multilayer]"]
  1-2-3-4-5-6-7-8_Layer = mystery part, 8 pins [chip_label=layer]
  C10 = Electrolytic Capacitor [capacitance=10µF voltage=10V package="100 mil [THT, electrolytic]"]

nets:
  5V: BLUEPILL.5V, UDN2981.Vcc, C10.+
  GND: BLUEPILL.G, BLUEPILL.GND, UDN2981.GND, 74HC595-L.GND, ULN2803-3.0V, 74HC595-3.GND, C5.0, ULN2803-4.0V, 74HC595-4.GND, C6.0, ULN2803-5.0V, 74HC595-5.GND, C7.1, ULN2803-6.0V, 74HC595-6.GND, C3.1, ULN2803-1.0V, 74HC595-1.GND, C4.1, ULN2803-2.0V, 74HC595-2.GND, C2.1, C9.-, C8.1, C10.-
  VCC: BLUEPILL.3.3V, BLUEPILL.3.3, 74HC595-L.MR, 74HC595-L.VCC, 74HC595-3.MR, 74HC595-3.VCC, C5.1, 74HC595-4.MR, 74HC595-4.VCC, C6.1, 74HC595-5.MR, 74HC595-5.VCC, C7.0, 74HC595-6.MR, 74HC595-6.VCC, C3.0, 74HC595-1.MR, 74HC595-1.VCC, C4.0, 74HC595-2.MR, 74HC595-2.VCC, C2.0, C9.+, C8.0
  N1: BLUEPILL.A0, 74HC595-L.OE, 74HC595-3.OE, 74HC595-4.OE, 74HC595-5.OE, 74HC595-6.OE, 74HC595-1.OE, 74HC595-2.OE
  N2: BLUEPILL.A1, 74HC595-L.ST_CP, 74HC595-3.ST_CP, 74HC595-4.ST_CP, 74HC595-5.ST_CP, 74HC595-6.ST_CP, 74HC595-1.ST_CP, 74HC595-2.ST_CP
  N3: BLUEPILL.A5, 74HC595-L.SH_CP, 74HC595-3.SH_CP, 74HC595-4.SH_CP, 74HC595-5.SH_CP, 74HC595-6.SH_CP, 74HC595-1.SH_CP, 74HC595-2.SH_CP
  N4: BLUEPILL.A7, 74HC595-L.DS
  N5: UDN2981.In_1, 74HC595-L.Q7
  N6: UDN2981.In_2, 74HC595-L.Q6
  N7: UDN2981.In_3, 74HC595-L.Q5
  N8: UDN2981.In_4, 74HC595-L.Q4
  N9: UDN2981.In_5, 74HC595-L.Q3
  N10: UDN2981.In_6, 74HC595-L.Q2
  N11: UDN2981.In_7, 74HC595-L.Q1
  N12: UDN2981.In_8, 74HC595-L.Q0
  N13: UDN2981.Out_8, 1-2-3-4-5-6-7-8_Layer.pin1
  N14: UDN2981.Out_7, 1-2-3-4-5-6-7-8_Layer.pin2
  N15: UDN2981.Out_6, 1-2-3-4-5-6-7-8_Layer.pin3
  N16: UDN2981.Out_5, 1-2-3-4-5-6-7-8_Layer.pin4
  N17: UDN2981.Out_4, 1-2-3-4-5-6-7-8_Layer.pin5
  N18: UDN2981.Out_3, 1-2-3-4-5-6-7-8_Layer.pin6
  N19: UDN2981.Out_2, 1-2-3-4-5-6-7-8_Layer.pin7
  N20: UDN2981.Out_1, 1-2-3-4-5-6-7-8_Layer.pin8
  N21: 74HC595-L.Q7', 74HC595-1.DS
  N22: ULN2803-3.In_1, 74HC595-3.Q7
  N23: ULN2803-3.In_2, 74HC595-3.Q6
  N24: ULN2803-3.In_3, 74HC595-3.Q5
  N25: ULN2803-3.In_4, 74HC595-3.Q4
  N26: ULN2803-3.In_5, 74HC595-3.Q3
  N27: ULN2803-3.In_6, 74HC595-3.Q2
  N28: ULN2803-3.In_7, 74HC595-3.Q1
  N29: ULN2803-3.In_8, 74HC595-3.Q0
  N30: ULN2803-3.Out_8, G0-0.Pin_0
  N31: ULN2803-3.Out_7, G0-1.Pin_0
  N32: ULN2803-3.Out_6, G0-2.Pin_0
  N33: ULN2803-3.Out_5, G0-3.Pin_0
  N34: ULN2803-3.Out_4, G1-0.Pin_0
  N35: ULN2803-3.Out_3, G1-1.Pin_0
  N36: ULN2803-3.Out_2, G1-2.Pin_0
  N37: ULN2803-3.Out_1, G1-3.Pin_0
  N38: G0-0.Pin_1, <G.pin1
  N39: 74HC595-3.Q7', 74HC595-4.DS
  N40: 74HC595-3.DS, 74HC595-2.Q7'
  N41: ULN2803-4.In_1, 74HC595-4.Q7
  N42: ULN2803-4.In_2, 74HC595-4.Q6
  N43: ULN2803-4.In_3, 74HC595-4.Q5
  N44: ULN2803-4.In_4, 74HC595-4.Q4
  N45: ULN2803-4.In_5, 74HC595-4.Q3
  N46: ULN2803-4.In_6, 74HC595-4.Q2
  N47: ULN2803-4.In_7, 74HC595-4.Q1
  N48: ULN2803-4.In_8, 74HC595-4.Q0
  N49: ULN2803-4.Out_8, G2-0.Pin_0
  N50: ULN2803-4.Out_7, G2-1.Pin_0
  N51: ULN2803-4.Out_6, G2-2.Pin_0
  N52: ULN2803-4.Out_5, G2-3.Pin_0
  N53: ULN2803-4.Out_4, G3-0.Pin_0
  N54: ULN2803-4.Out_3, G3-1.Pin_0
  N55: ULN2803-4.Out_2, G3-2.Pin_0
  N56: ULN2803-4.Out_1, G3-3.Pin_0
  N57: 74HC595-4.Q7', 74HC595-5.DS
  N58: ULN2803-5.In_1, 74HC595-5.Q7
  N59: ULN2803-5.In_2, 74HC595-5.Q6
  N60: ULN2803-5.In_3, 74HC595-5.Q5
  N61: ULN2803-5.In_4, 74HC595-5.Q4
  N62: ULN2803-5.In_5, 74HC595-5.Q3
  N63: ULN2803-5.In_6, 74HC595-5.Q2
  N64: ULN2803-5.In_7, 74HC595-5.Q1
  N65: ULN2803-5.In_8, 74HC595-5.Q0
  N66: ULN2803-5.Out_8, B0-0.Pin_1
  N67: ULN2803-5.Out_7, B0-1.Pin_1
  N68: ULN2803-5.Out_6, B0-2.Pin_1
  N69: ULN2803-5.Out_5, B0-3.Pin_1
  N70: ULN2803-5.Out_4, B1-0.Pin_1
  N71: ULN2803-5.Out_3, B1-1.Pin_1
  N72: ULN2803-5.Out_2, B1-2.Pin_1
  N73: ULN2803-5.Out_1, B1-3.Pin_1
  N74: 74HC595-5.Q7', 74HC595-6.DS
  N75: ULN2803-6.In_1, 74HC595-6.Q7
  N76: ULN2803-6.In_2, 74HC595-6.Q6
  N77: ULN2803-6.In_3, 74HC595-6.Q5
  N78: ULN2803-6.In_4, 74HC595-6.Q4
  N79: ULN2803-6.In_5, 74HC595-6.Q3
  N80: ULN2803-6.In_6, 74HC595-6.Q2
  N81: ULN2803-6.In_7, 74HC595-6.Q1
  N82: ULN2803-6.In_8, 74HC595-6.Q0
  N83: ULN2803-6.Out_8, B2-0.Pin_1
  N84: ULN2803-6.Out_7, B2-1.Pin_1
  N85: ULN2803-6.Out_6, B2-2.Pin_1
  N86: ULN2803-6.Out_5, B2-3.Pin_1
  N87: ULN2803-6.Out_4, B3-1.Pin_1
  N88: ULN2803-6.Out_3, B3-1_2.Pin_1
  N89: ULN2803-6.Out_2, B3-2.Pin_1
  N90: ULN2803-6.Out_1, B3-3.Pin_1
  N91: ULN2803-1.In_1, 74HC595-1.Q7
  N92: ULN2803-1.In_2, 74HC595-1.Q6
  N93: ULN2803-1.In_3, 74HC595-1.Q5
  N94: ULN2803-1.In_4, 74HC595-1.Q4
  N95: ULN2803-1.In_5, 74HC595-1.Q3
  N96: ULN2803-1.In_6, 74HC595-1.Q2
  N97: ULN2803-1.In_7, 74HC595-1.Q1
  N98: ULN2803-1.In_8, 74HC595-1.Q0
  N99: ULN2803-1.Out_8, R0-0.Pin_0
  N100: ULN2803-1.Out_7, R0-1.Pin_0
  N101: ULN2803-1.Out_6, R0-2.Pin_0
  N102: ULN2803-1.Out_5, R0-3.Pin_0
  N103: ULN2803-1.Out_4, R1-0.Pin_0
  N104: ULN2803-1.Out_3, R1-1.Pin_0
  N105: ULN2803-1.Out_2, R1-2.Pin_0
  N106: ULN2803-1.Out_1, R1-3.Pin_0
  N107: R0-0.Pin_1, <RED.pin1
  N108: 74HC595-1.Q7', 74HC595-2.DS
  N109: ULN2803-2.In_1, 74HC595-2.Q7
  N110: ULN2803-2.In_2, 74HC595-2.Q6
  N111: ULN2803-2.In_3, 74HC595-2.Q5
  N112: ULN2803-2.In_4, 74HC595-2.Q4
  N113: ULN2803-2.In_5, 74HC595-2.Q3
  N114: ULN2803-2.In_6, 74HC595-2.Q2
  N115: ULN2803-2.In_7, 74HC595-2.Q1
  N116: ULN2803-2.In_8, 74HC595-2.Q0
  N117: ULN2803-2.Out_8, R2-0.Pin_0
  N118: ULN2803-2.Out_7, R2-1.Pin_0
  N119: ULN2803-2.Out_6, R2-2.Pin_0
  N120: ULN2803-2.Out_5, R2-3.Pin_0
  N121: ULN2803-2.Out_4, R3-0.Pin_0
  N122: ULN2803-2.Out_3, R3-1.Pin_0
  N123: ULN2803-2.Out_2, R3-2.Pin_0
  N124: ULN2803-2.Out_1, R3-3.Pin_0
  N125: R0-1.Pin_1, <RED.pin2
  N126: R0-2.Pin_1, <RED.pin3
  N127: R0-3.Pin_1, <RED.pin4
  N128: R1-0.Pin_1, <-RED4.pin1
  N129: R1-1.Pin_1, <-RED4.pin2
  N130: R1-2.Pin_1, <-RED4.pin3
  N131: R1-3.Pin_1, <-RED4.pin4
  N132: <R.pin1, R2-0.Pin_1
  N133: <R.pin2, R2-1.Pin_1
  N134: <R.pin3, R2-2.Pin_1
  N135: <R.pin4, R2-3.Pin_1
  N136: <-RED5.pin1, R3-0.Pin_1
  N137: <-RED5.pin2, R3-1.Pin_1
  N138: <-RED5.pin3, R3-2.Pin_1
  N139: <-RED5.pin4, R3-3.Pin_1
  N140: G0-1.Pin_1, <G.pin2
  N141: G0-2.Pin_1, <G.pin3
  N142: G0-3.Pin_1, <G.pin4
  N143: G1-0.Pin_1, <-G1.pin1
  N144: G1-1.Pin_1, <-G1.pin2
  N145: G1-2.Pin_1, <-G1.pin3
  N146: G1-3.Pin_1, <-G1.pin4
  N147: G2-0.Pin_1, <G1.pin1
  N148: G3-1.Pin_1, <-G2.pin2
  N149: G2-2.Pin_1, <G1.pin3
  N150: G2-3.Pin_1, <G1.pin4
  N151: G3-0.Pin_1, <-G2.pin1
  N152: G3-2.Pin_1, <-G2.pin3
  N153: G2-1.Pin_1, <G1.pin2
  N154: G3-3.Pin_1, <-G2.pin4
  N155: BLUE>.pin1, B0-0.Pin_0
  N156: BLUE>.pin2, B0-1.Pin_0
  N157: BLUE>.pin3, B0-2.Pin_0
  N158: BLUE>.pin4, B0-3.Pin_0
  N159: <-RED6.pin1, B1-0.Pin_0
  N160: <-RED6.pin2, B1-1.Pin_0
  N161: <-RED6.pin3, B1-2.Pin_0
  N162: <-RED6.pin4, B1-3.Pin_0
  N163: B2-2.Pin_0, <-RED7.pin3
  N164: B3-3.Pin_0, <-RED8.pin4
  N165: B3-1.Pin_0, <-RED8.pin1
  N166: B2-3.Pin_0, <-RED7.pin4
  N167: B3-1_2.Pin_0, <-RED8.pin2
  N168: B2-0.Pin_0, <-RED7.pin1
  N169: B2-1.Pin_0, <-RED7.pin2
  N170: B3-2.Pin_0, <-RED8.pin3

notes:
  VCC
  CLOCK
  /OE
  LATCH
  GND
  OUT
  Bakisha2018
  74HC595
  C
  VCC 5V
  USB
  PA1 - LE
  PA0 - OE/
  PA7 -MOSI
  PA5 -CLK
  16x
  470Ω
  330Ω
  C2-C8
  4x4x8 BLUEPILL  RGB CUBE
  100nF
  Design -  BAKISHA 2019
  USCL cube(4, 4, 8, RGB_CUBE , PA0, PA1, 60 , 4, SPI_speed_8);

custom parts:
  STM32F103C8T6 blue mini board: Generic Blue Pill microcomputer module, available from Ebay and others. CPU STM32F103C8 72Mhz Flash: 64 KB/128 KB RAM: 20KB.
  DIP - 18 pins: Recommended for high-side switching applications that benefit from separate logic and load grounds, these devices encompass load supply voltages to 50 V and output currents to -500 mA. These 8-channel source drivers are useful for interfacing between low-level logic and high-current loads. Typical loads include relays, solenoids, lamps, stepper and/or servo motors, print hammers, and LEDs.
