# Fritzing sketch GREEN (saved by Fritzing 0.9.3b)
circuit board: 15cm x 10cm
breadboards: 1

parts:
  ULN2803-4 = ULN2803A [package=THT]
  U7 = 74HC595 [package="DIP16 [THT]"]
  R-4-1 = Resistor [tolerance=±5% resistance=220 package=THT]
  R-4-2 = Resistor [tolerance=±5% resistance=220 package=THT]
  R-4-3 = Resistor [tolerance=±5% resistance=220 package=THT]
  R-4-4 = Resistor [tolerance=±5% resistance=220 package=THT]
  R-4-5 = Resistor [tolerance=±5% resistance=220 package=THT]
  R-4-6 = Resistor [tolerance=±5% resistance=220 package=THT]
  R-4-7 = Resistor [tolerance=±5% resistance=220 package=THT]
  R-4-0 = Resistor [tolerance=±5% resistance=220 package=THT]
  ULN2803-5 = ULN2803A [package=THT]
  U8 = 74HC595 [package="DIP16 [THT]"]
  R-5-1 = Resistor [tolerance=±5% resistance=220 package=THT]
  R-5-2 = Resistor [tolerance=±5% resistance=220 package=THT]
  R-5-3 = Resistor [tolerance=±5% resistance=220 package=THT]
  R-5-4 = Resistor [tolerance=±5% resistance=220 package=THT]
  R-5-5 = Resistor [tolerance=±5% resistance=220 package=THT]
  R-5-6 = Resistor [tolerance=±5% resistance=220 package=THT]
  R-5-7 = Resistor [tolerance=±5% resistance=220 package=THT]
  R-5-0 = Resistor [tolerance=±5% resistance=220 package=THT]
  ULN2803-6 = ULN2803A [package=THT]
  U9 = 74HC595 [package="DIP16 [THT]"]
  R-6-1 = Resistor [tolerance=±5% resistance=220 package=THT]
  R-6-2 = Resistor [tolerance=±5% resistance=220 package=THT]
  R-6-3 = Resistor [tolerance=±5% resistance=220 package=THT]
  R-6-4 = Resistor [tolerance=±5% resistance=220 package=THT]
  R-6-5 = Resistor [tolerance=±5% resistance=220 package=THT]
  R-6-6 = Resistor [tolerance=±5% resistance=220 package=THT]
  R-6-7 = Resistor [tolerance=±5% resistance=220 package=THT]
  R-6-0 = Resistor [tolerance=±5% resistance=220 package=THT]
  ULN2803-7 = ULN2803A [package=THT]
  U10 = 74HC595 [package="DIP16 [THT]"]
  R-7-1 = Resistor [tolerance=±5% resistance=220 package=THT]
  R-7-2 = Resistor [tolerance=±5% resistance=220 package=THT]
  R-7-3 = Resistor [tolerance=±5% resistance=220 package=THT]
  R-7-4 = Resistor [tolerance=±5% resistance=220 package=THT]
  R-7-5 = Resistor [tolerance=±5% resistance=220 package=THT]
  R-7-6 = Resistor [tolerance=±5% resistance=220 package=THT]
  R-7-7 = Resistor [tolerance=±5% resistance=220 package=THT]
  R-7-0 = Resistor [tolerance=±5% resistance=220 package=THT]
  ULN2803-3 = ULN2803A [package=THT]
  U11 = 74HC595 [package="DIP16 [THT]"]
  R-3-2 = Resistor [tolerance=±5% resistance=220 package=THT]
  R-3-3 = Resistor [tolerance=±5% resistance=220 package=THT]
  R-3-4 = Resistor [tolerance=±5% resistance=220 package=THT]
  R-3-5 = Resistor [tolerance=±5% resistance=220 package=THT]
  R-3-6 = Resistor [tolerance=±5% resistance=220 package=THT]
  R-3-7 = Resistor [tolerance=±5% resistance=220 package=THT]
  R-3-1 = Resistor [tolerance=±5% resistance=220 package=THT]
  R-3-0 = Resistor [tolerance=±5% resistance=220 package=THT]
  ULN2803-2 = ULN2803A [package=THT]
  U12 = 74HC595 [package="DIP16 [THT]"]
  R-2-2 = Resistor [tolerance=±5% resistance=220 package=THT]
  R-2-3 = Resistor [tolerance=±5% resistance=220 package=THT]
  R-2-4 = Resistor [tolerance=±5% resistance=220 package=THT]
  R-2-5 = Resistor [tolerance=±5% resistance=220 package=THT]
  R-2-6 = Resistor [tolerance=±5% resistance=220 package=THT]
  R-2-7 = Resistor [tolerance=±5% resistance=220 package=THT]
  R-2-1 = Resistor [tolerance=±5% resistance=220 package=THT]
  R-2-0 = Resistor [tolerance=±5% resistance=220 package=THT]
  ULN2803-1 = ULN2803A [package=THT]
  U13 = 74HC595 [package="DIP16 [THT]"]
  R-1-2 = Resistor [tolerance=±5% resistance=220 package=THT]
  R-1-3 = Resistor [tolerance=±5% resistance=220 package=THT]
  R-1-4 = Resistor [tolerance=±5% resistance=220 package=THT]
  R-1-5 = Resistor [tolerance=±5% resistance=220 package=THT]
  R-1-6 = Resistor [tolerance=±5% resistance=220 package=THT]
  R-1-7 = Resistor [tolerance=±5% resistance=220 package=THT]
  R-1-1 = Resistor [tolerance=±5% resistance=220 package=THT]
  R-1-0 = Resistor [tolerance=±5% resistance=220 package=THT]
  ULN2803-0 = ULN2803A [package=THT]
  U14 = 74HC595 [package="DIP16 [THT]"]
  R-0-2 = Resistor [tolerance=±5% resistance=220 package=THT]
  R-0-3 = Resistor [tolerance=±5% resistance=220 package=THT]
  R-0-4 = Resistor [tolerance=±5% resistance=220 package=THT]
  R-0-5 = Resistor [tolerance=±5% resistance=220 package=THT]
  R-0-6 = Resistor [tolerance=±5% resistance=220 package=THT]
  R-0-7 = Resistor [tolerance=±5% resistance=220 package=THT]
  R-0-1 = Resistor [tolerance=±5% resistance=220 package=THT]
  R-0-0 = Resistor [tolerance=±5% resistance=220 package=THT]
  C1 = Electrolytic Capacitor [capacitance=10µF package="300 mil [THT, electrolytic]"]
  C2 = Electrolytic Capacitor [capacitance=10µF package="300 mil [THT, electrolytic]"]
  J11 = screw terminal, 2 pins
  GREEN_-_IN = mystery part, 4 pins [chip_label=?]
  GREEN_-_OUT = mystery part, 4 pins [chip_label=?]
  B4 = mystery part, 8 pins [chip_label=?]
  B3 = mystery part, 8 pins [chip_label=?]
  B5 = mystery part, 8 pins [chip_label=?]
  B2 = mystery part, 8 pins [chip_label=?]
  B6 = mystery part, 8 pins [chip_label=?]
  B7 = mystery part, 8 pins [chip_label=?]
  B1 = mystery part, 8 pins [chip_label=?]
  B0 = mystery part, 8 pins [chip_label=?]

nets:
  N1: ULN2803-4.In_1, U7.Q7
  N2: ULN2803-4.In_2, U7.Q6
  N3: ULN2803-4.In_3, U7.Q5
  N4: ULN2803-4.In_4, U7.Q4
  N5: ULN2803-4.In_5, U7.Q3
  N6: ULN2803-4.In_6, U7.Q2
  N7: ULN2803-4.In_7, U7.Q1
  N8: ULN2803-4.In_8, U7.Q0
  GND: ULN2803-4.0V, U7.GND, ULN2803-5.0V, U8.GND, ULN2803-6.0V, U9.GND, ULN2803-7.0V, U10.GND, ULN2803-3.0V, U11.GND, ULN2803-2.0V, U12.GND, ULN2803-1.0V, U13.GND, ULN2803-0.0V, U14.GND, C1.-, C2.-, J11.pin2
  N9: ULN2803-4.Out_8, R-4-0.Pin_0
  N10: ULN2803-4.Out_7, R-4-1.Pin_0
  N11: ULN2803-4.Out_6, R-4-2.Pin_0
  N12: ULN2803-4.Out_5, R-4-3.Pin_0
  N13: ULN2803-4.Out_4, R-4-4.Pin_0
  N14: ULN2803-4.Out_3, R-4-5.Pin_0
  N15: ULN2803-4.Out_2, R-4-6.Pin_0
  N16: ULN2803-4.Out_1, R-4-7.Pin_0
  N17: U7.Q7', U8.DS
  VCC: U7.MR, U7.VCC, U8.MR, U8.VCC, U9.MR, U9.VCC, U10.MR, U10.VCC, U11.MR, U11.VCC, U12.MR, U12.VCC, U13.MR, U13.VCC, U14.MR, U14.VCC, C1.+, C2.+, J11.pin1
  N18: U7.SH_CP, U8.SH_CP, U9.SH_CP, U10.SH_CP, U11.SH_CP, U12.SH_CP, U13.SH_CP, U14.SH_CP, GREEN_-_IN.pin1, GREEN_-_OUT.pin1
  N19: U7.ST_CP, U8.ST_CP, U9.ST_CP, U10.ST_CP, U11.ST_CP, U12.ST_CP, U13.ST_CP, U14.ST_CP, GREEN_-_IN.pin3, GREEN_-_OUT.pin3
  N20: U7.OE, U8.OE, U9.OE, U10.OE, U11.OE, U12.OE, U13.OE, U14.OE, GREEN_-_IN.pin2, GREEN_-_OUT.pin2
  N21: U7.DS, U11.Q7'
  N22: R-4-1.Pin_1, B4.pin2
  N23: R-4-2.Pin_1, B4.pin3
  N24: R-4-3.Pin_1, B4.pin4
  N25: R-4-4.Pin_1, B4.pin5
  N26: R-4-5.Pin_1, B4.pin6
  N27: R-4-6.Pin_1, B4.pin7
  N28: R-4-7.Pin_1, B4.pin8
  N29: R-4-0.Pin_1, B4.pin1
  N30: ULN2803-5.In_1, U8.Q7
  N31: ULN2803-5.In_2, U8.Q6
  N32: ULN2803-5.In_3, U8.Q5
  N33: ULN2803-5.In_4, U8.Q4
  N34: ULN2803-5.In_5, U8.Q3
  N35: ULN2803-5.In_6, U8.Q2
  N36: ULN2803-5.In_7, U8.Q1
  N37: ULN2803-5.In_8, U8.Q0
  N38: ULN2803-5.Out_8, R-5-0.Pin_0
  N39: ULN2803-5.Out_7, R-5-1.Pin_0
  N40: ULN2803-5.Out_6, R-5-2.Pin_0
  N41: ULN2803-5.Out_5, R-5-3.Pin_0
  N42: ULN2803-5.Out_4, R-5-4.Pin_0
  N43: ULN2803-5.Out_3, R-5-5.Pin_0
  N44: ULN2803-5.Out_2, R-5-6.Pin_0
  N45: ULN2803-5.Out_1, R-5-7.Pin_0
  N46: U8.Q7', U9.DS
  N47: R-5-1.Pin_1, B5.pin2
  N48: R-5-2.Pin_1, B5.pin3
  N49: R-5-3.Pin_1, B5.pin4
  N50: R-5-4.Pin_1, B5.pin5
  N51: R-5-5.Pin_1, B5.pin6
  N52: R-5-6.Pin_1, B5.pin7
  N53: R-5-7.Pin_1, B5.pin8
  N54: R-5-0.Pin_1, B5.pin1
  N55: ULN2803-6.In_1, U9.Q7
  N56: ULN2803-6.In_2, U9.Q6
  N57: ULN2803-6.In_3, U9.Q5
  N58: ULN2803-6.In_4, U9.Q4
  N59: ULN2803-6.In_5, U9.Q3
  N60: ULN2803-6.In_6, U9.Q2
  N61: ULN2803-6.In_7, U9.Q1
  N62: ULN2803-6.In_8, U9.Q0
  N63: ULN2803-6.Out_8, R-6-0.Pin_0
  N64: ULN2803-6.Out_7, R-6-1.Pin_0
  N65: ULN2803-6.Out_6, R-6-2.Pin_0
  N66: ULN2803-6.Out_5, R-6-3.Pin_0
  N67: ULN2803-6.Out_4, R-6-4.Pin_0
  N68: ULN2803-6.Out_3, R-6-5.Pin_0
  N69: ULN2803-6.Out_2, R-6-6.Pin_0
  N70: ULN2803-6.Out_1, R-6-7.Pin_0
  N71: U9.Q7', U10.DS
  N72: R-6-1.Pin_1, B6.pin2
  N73: R-6-2.Pin_1, B6.pin3
  N74: R-6-3.Pin_1, B6.pin4
  N75: R-6-4.Pin_1, B6.pin5
  N76: R-6-5.Pin_1, B6.pin6
  N77: R-6-6.Pin_1, B6.pin7
  N78: R-6-7.Pin_1, B6.pin8
  N79: R-6-0.Pin_1, B6.pin1
  N80: ULN2803-7.In_1, U10.Q7
  N81: ULN2803-7.In_2, U10.Q6
  N82: ULN2803-7.In_3, U10.Q5
  N83: ULN2803-7.In_4, U10.Q4
  N84: ULN2803-7.In_5, U10.Q3
  N85: ULN2803-7.In_6, U10.Q2
  N86: ULN2803-7.In_7, U10.Q1
  N87: ULN2803-7.In_8, U10.Q0
  N88: ULN2803-7.Out_8, R-7-0.Pin_0
  N89: ULN2803-7.Out_7, R-7-1.Pin_0
  N90: ULN2803-7.Out_6, R-7-2.Pin_0
  N91: ULN2803-7.Out_5, R-7-3.Pin_0
  N92: ULN2803-7.Out_4, R-7-4.Pin_0
  N93: ULN2803-7.Out_3, R-7-5.Pin_0
  N94: ULN2803-7.Out_2, R-7-6.Pin_0
  N95: ULN2803-7.Out_1, R-7-7.Pin_0
  N96: U10.Q7', GREEN_-_OUT.pin4
  N97: R-7-1.Pin_1, B7.pin2
  N98: R-7-2.Pin_1, B7.pin3
  N99: R-7-3.Pin_1, B7.pin4
  N100: R-7-4.Pin_1, B7.pin5
  N101: R-7-5.Pin_1, B7.pin6
  N102: R-7-6.Pin_1, B7.pin7
  N103: R-7-7.Pin_1, B7.pin8
  N104: R-7-0.Pin_1, B7.pin1
  N105: ULN2803-3.In_1, U11.Q7
  N106: ULN2803-3.In_2, U11.Q6
  N107: ULN2803-3.In_3, U11.Q5
  N108: ULN2803-3.In_4, U11.Q4
  N109: ULN2803-3.In_5, U11.Q3
  N110: ULN2803-3.In_6, U11.Q2
  N111: ULN2803-3.In_7, U11.Q1
  N112: ULN2803-3.In_8, U11.Q0
  N113: ULN2803-3.Out_8, R-3-0.Pin_0
  N114: ULN2803-3.Out_7, R-3-1.Pin_0
  N115: ULN2803-3.Out_6, R-3-2.Pin_0
  N116: ULN2803-3.Out_5, R-3-3.Pin_0
  N117: ULN2803-3.Out_4, R-3-4.Pin_0
  N118: ULN2803-3.Out_3, R-3-5.Pin_0
  N119: ULN2803-3.Out_2, R-3-6.Pin_0
  N120: ULN2803-3.Out_1, R-3-7.Pin_0
  N121: U11.DS, U12.Q7'
  N122: R-3-2.Pin_1, B3.pin6
  N123: R-3-3.Pin_1, B3.pin5
  N124: R-3-4.Pin_1, B3.pin4
  N125: R-3-5.Pin_1, B3.pin3
  N126: R-3-6.Pin_1, B3.pin2
  N127: R-3-7.Pin_1, B3.pin1
  N128: R-3-1.Pin_1, B3.pin7
  N129: R-3-0.Pin_1, B3.pin8
  N130: ULN2803-2.In_1, U12.Q7
  N131: ULN2803-2.In_2, U12.Q6
  N132: ULN2803-2.In_3, U12.Q5
  N133: ULN2803-2.In_4, U12.Q4
  N134: ULN2803-2.In_5, U12.Q3
  N135: ULN2803-2.In_6, U12.Q2
  N136: ULN2803-2.In_7, U12.Q1
  N137: ULN2803-2.In_8, U12.Q0
  N138: ULN2803-2.Out_8, R-2-0.Pin_0
  N139: ULN2803-2.Out_7, R-2-1.Pin_0
  N140: ULN2803-2.Out_6, R-2-2.Pin_0
  N141: ULN2803-2.Out_5, R-2-3.Pin_0
  N142: ULN2803-2.Out_4, R-2-4.Pin_0
  N143: ULN2803-2.Out_3, R-2-5.Pin_0
  N144: ULN2803-2.Out_2, R-2-6.Pin_0
  N145: ULN2803-2.Out_1, R-2-7.Pin_0
  N146: U12.DS, U13.Q7'
  N147: R-2-2.Pin_1, B2.pin6
  N148: R-2-3.Pin_1, B2.pin5
  N149: R-2-4.Pin_1, B2.pin4
  N150: R-2-5.Pin_1, B2.pin3
  N151: R-2-6.Pin_1, B2.pin2
  N152: R-2-7.Pin_1, B2.pin1
  N153: R-2-1.Pin_1, B2.pin7
  N154: R-2-0.Pin_1, B2.pin8
  N155: ULN2803-1.In_1, U13.Q7
  N156: ULN2803-1.In_2, U13.Q6
  N157: ULN2803-1.In_3, U13.Q5
  N158: ULN2803-1.In_4, U13.Q4
  N159: ULN2803-1.In_5, U13.Q3
  N160: ULN2803-1.In_6, U13.Q2
  N161: ULN2803-1.In_7, U13.Q1
  N162: ULN2803-1.In_8, U13.Q0
  N163: ULN2803-1.Out_8, R-1-0.Pin_0
  N164: ULN2803-1.Out_7, R-1-1.Pin_0
  N165: ULN2803-1.Out_6, R-1-2.Pin_0
  N166: ULN2803-1.Out_5, R-1-3.Pin_0
  N167: ULN2803-1.Out_4, R-1-4.Pin_0
  N168: ULN2803-1.Out_3, R-1-5.Pin_0
  N169: ULN2803-1.Out_2, R-1-6.Pin_0
  N170: ULN2803-1.Out_1, R-1-7.Pin_0
  N171: U13.DS, U14.Q7'
  N172: R-1-2.Pin_1, B1.pin6
  N173: R-1-3.Pin_1, B1.pin5
  N174: R-1-4.Pin_1, B1.pin4
  N175: R-1-5.Pin_1, B1.pin3
  N176: R-1-6.Pin_1, B1.pin2
  N177: R-1-7.Pin_1, B1.pin1
  N178: R-1-1.Pin_1, B1.pin7
  N179: R-1-0.Pin_1, B1.pin8
  N180: ULN2803-0.In_1, U14.Q7
  N181: ULN2803-0.In_2, U14.Q6
  N182: ULN2803-0.In_3, U14.Q5
  N183: ULN2803-0.In_4, U14.Q4
  N184: ULN2803-0.In_5, U14.Q3
  N185: ULN2803-0.In_6, U14.Q2
  N186: ULN2803-0.In_7, U14.Q1
  N187: ULN2803-0.In_8, U14.Q0
  N188: ULN2803-0.Out_8, R-0-0.Pin_0
  N189: ULN2803-0.Out_7, R-0-1.Pin_0
  N190: ULN2803-0.Out_6, R-0-2.Pin_0
  N191: ULN2803-0.Out_5, R-0-3.Pin_0
  N192: ULN2803-0.Out_4, R-0-4.Pin_0
  N193: ULN2803-0.Out_3, R-0-5.Pin_0
  N194: ULN2803-0.Out_2, R-0-6.Pin_0
  N195: ULN2803-0.Out_1, R-0-7.Pin_0
  N196: U14.DS, GREEN_-_IN.pin4
  N197: R-0-2.Pin_1, B0.pin6
  N198: R-0-3.Pin_1, B0.pin5
  N199: R-0-4.Pin_1, B0.pin4
  N200: R-0-5.Pin_1, B0.pin3
  N201: R-0-6.Pin_1, B0.pin2
  N202: R-0-7.Pin_1, B0.pin1
  N203: R-0-1.Pin_1, B0.pin7
  N204: R-0-0.Pin_1, B0.pin8

notes:
  VCC
  CLOCK
  /OE
  LATCH
  GND
  OUT
  VCC + 3.3V
  CLK
  LE
  DATA_IN
  Bakisha2018
  74HC595
  C
  DATA_OUT
