# Fritzing sketch IDE cable to CUBE (saved by Fritzing 0.9.3b)
circuit board: 12cm x 15cm
breadboards: 1

parts:
  IDE_-_levo = mystery part, 40 pins [chip_label=?]
  B4 = mystery part, 8 pins [chip_label=?]
  B3 = mystery part, 8 pins [chip_label=?]
  B5 = mystery part, 8 pins [chip_label=?]
  B2 = mystery part, 8 pins [chip_label=?]
  B0 = mystery part, 8 pins [chip_label=?]
  B7 = mystery part, 8 pins [chip_label=?]
  B1 = mystery part, 8 pins [chip_label=?]
  B6 = mystery part, 8 pins [chip_label=?]
  IDE_-_desno = mystery part, 40 pins [chip_label=?]

nets:
  N1: IDE_-_levo.pin1, B4.pin1
  N2: IDE_-_levo.pin2, B3.pin1
  N3: IDE_-_levo.pin3, B4.pin2
  N4: IDE_-_levo.pin4, B3.pin2
  N5: IDE_-_levo.pin5, B4.pin3
  N6: IDE_-_levo.pin6, B3.pin3
  N7: IDE_-_levo.pin7, B4.pin4
  N8: IDE_-_levo.pin8, B3.pin4
  N9: IDE_-_levo.pin9, B4.pin5
  N10: IDE_-_levo.pin10, B3.pin5
  N11: IDE_-_levo.pin11, B4.pin6
  N12: IDE_-_levo.pin12, B3.pin6
  N13: IDE_-_levo.pin13, B4.pin7
  N14: IDE_-_levo.pin14, B3.pin7
  N15: IDE_-_levo.pin15, B4.pin8
  N16: IDE_-_levo.pin16, B3.pin8
  N17: IDE_-_levo.pin25, B5.pin1
  N18: IDE_-_levo.pin26, B2.pin1
  N19: IDE_-_levo.pin27, B5.pin2
  N20: IDE_-_levo.pin28, B2.pin2
  N21: IDE_-_levo.pin29, B5.pin3
  N22: IDE_-_levo.pin30, B2.pin3
  N23: IDE_-_levo.pin31, B5.pin4
  N24: IDE_-_levo.pin32, B2.pin4
  N25: IDE_-_levo.pin33, B5.pin5
  N26: IDE_-_levo.pin34, B2.pin5
  N27: IDE_-_levo.pin35, B5.pin6
  N28: IDE_-_levo.pin36, B2.pin6
  N29: IDE_-_levo.pin37, B5.pin7
  N30: IDE_-_levo.pin38, B2.pin7
  N31: IDE_-_levo.pin39, B5.pin8
  N32: IDE_-_levo.pin40, B2.pin8
  N33: B0.pin1, IDE_-_desno.pin26
  N34: B0.pin2, IDE_-_desno.pin28
  N35: B0.pin3, IDE_-_desno.pin30
  N36: B0.pin4, IDE_-_desno.pin32
  N37: B0.pin5, IDE_-_desno.pin34
  N38: B0.pin6, IDE_-_desno.pin36
  N39: B0.pin7, IDE_-_desno.pin38
  N40: B0.pin8, IDE_-_desno.pin40
  N41: B7.pin1, IDE_-_desno.pin25
  N42: B7.pin2, IDE_-_desno.pin27
  N43: B7.pin3, IDE_-_desno.pin29
  N44: B7.pin4, IDE_-_desno.pin31
  N45: B7.pin5, IDE_-_desno.pin33
  N46: B7.pin6, IDE_-_desno.pin35
  N47: B7.pin7, IDE_-_desno.pin37
  N48: B7.pin8, IDE_-_desno.pin39
  N49: B1.pin1, IDE_-_desno.pin2
  N50: B1.pin2, IDE_-_desno.pin4
  N51: B1.pin3, IDE_-_desno.pin6
  N52: B1.pin4, IDE_-_desno.pin8
  N53: B1.pin5, IDE_-_desno.pin10
  N54: B1.pin6, IDE_-_desno.pin12
  N55: B1.pin7, IDE_-_desno.pin14
  N56: B1.pin8, IDE_-_desno.pin16
  N57: B6.pin1, IDE_-_desno.pin1
  N58: B6.pin2, IDE_-_desno.pin3
  N59: B6.pin3, IDE_-_desno.pin5
  N60: B6.pin4, IDE_-_desno.pin7
  N61: B6.pin5, IDE_-_desno.pin9
  N62: B6.pin6, IDE_-_desno.pin11
  N63: B6.pin7, IDE_-_desno.pin13
  N64: B6.pin8, IDE_-_desno.pin15

notes:
  01 * 4-0
  03 * 4-1
  05 * 4-2
  07 * 4-3
  09 * 4-4
  11 * 4-5
  13 * 4-6
  15 * 4-7
  02 * 3-7
  04 * 3-6
  06 * 3-5
  08 * 3-4
  10 * 3-3
  12 * 3-2
  14 * 3-1
  16 * 3-0
  36 * 2-2
  27 * 5-1
  37 * 5-6
  30 * 2-5
  29 * 5-2
  34 * 2-3
  32 * 2-4
  38 * 2-1
  40 * 2-0
  33 * 5-4
  26 * 2-7
  35 * 5-5
  28 * 2-6
  39 * 5-7
  31 * 5-3
  25 * 5-0
  10 * 1-3
  15 * 6-7
  16 * 1-0
  28 * 0-6
  37 * 7-6
  39 * 7-7
  11 * 6-5
  30 * 0-5
  02 * 1-7
  32 * 0-4
  34 * 0-3
  26 * 0-7
  35 * 7-5
  05 * 6-2
  14 * 1-1
  03 * 6-1
  06 * 1-5
  31 * 7-3
  25 * 7-0
  09 * 6-4
  13 * 6-6
  29 * 7-2
  27 * 7-1
  07 * 6-3
  04 * 1-6
  08 * 1-4
  12 * 1-2
  38 * 0-1
  33 * 7-4
  36 * 0-2
  40 * 0-0
  01 * 6-0
