# Fritzing sketch RGB_595_HIGH_SIDE_BLUEPILL (saved by Fritzing 0.9.3b)
circuit board: 15cm x 10cm
breadboards: 1

parts:
  BluePill1 = IC, DIP package, 40 pins [chip_label=IC]
  ULN2803 = ULN2803A [package=THT]
  1K-Pullup_--> = mystery part, 9 pins [chip_label=?]
  Q8 = Basic FET P-Channel [package="TO220 [THT]"]
  Q7 = Basic FET P-Channel [package="TO220 [THT]"]
  Q6 = Basic FET P-Channel [package="TO220 [THT]"]
  Q5 = Basic FET P-Channel [package="TO220 [THT]"]
  Q4 = Basic FET P-Channel [package="TO220 [THT]"]
  Q3 = Basic FET P-Channel [package="TO220 [THT]"]
  Q2 = Basic FET P-Channel [package="TO220 [THT]"]
  Q1 = Basic FET P-Channel [package="TO220 [THT]"]
  74HC595 = 74HC595 [package="DIP16 [THT]"]
  74HC245 = 74LVC245 Octal 2-Way Tranceiver
  J3 = screw terminal, 2 pins
  J4 = screw terminal, 2 pins
  J5 = screw terminal, 2 pins
  J6 = screw terminal, 2 pins
  J7 = screw terminal, 2 pins
  J8 = screw terminal, 2 pins
  J9 = screw terminal, 2 pins
  IN-BLUE = mystery part, 4 pins [chip_label=?]
  OUT-BLUE = mystery part, 4 pins [chip_label=?]
  OUT-GREEN = mystery part, 4 pins [chip_label=?]
  IN-GREEN = mystery part, 4 pins [chip_label=?]
  IN-RED = mystery part, 4 pins [chip_label=?]
  J10 = screw terminal, 2 pins
  D1 = Diode [package=diode-1n4001]
  C2 = Electrolytic Capacitor [capacitance=10µF package="300 mil [THT, electrolytic]"]

nets:
  N1: BluePill1.pin18, D1.C
  GND: BluePill1.pin19, ULN2803.0V, 74HC595.GND, 74HC245.GND, 74HC245.!OE, J3.pin2, J4.pin2, J5.pin2, J10.pin1, C2.-
  VCC: BluePill1.pin20, 74HC595.MR, 74HC595.VCC, 74HC245.DIR, 74HC245.VCC, J3.pin1, J4.pin1, J5.pin1
  N2: BluePill1.pin25, 74HC595.OE, IN-BLUE.pin2
  N3: BluePill1.pin26, 74HC595.ST_CP, IN-BLUE.pin3
  N4: BluePill1.pin30, 74HC595.SH_CP, IN-BLUE.pin1
  N5: BluePill1.pin32, 74HC595.DS
  N6: ULN2803.In_1, 74HC595.Q7
  N7: ULN2803.In_2, 74HC595.Q6
  N8: ULN2803.In_3, 74HC595.Q5
  N9: ULN2803.In_4, 74HC595.Q4
  N10: ULN2803.In_5, 74HC595.Q3
  N11: ULN2803.In_6, 74HC595.Q2
  N12: ULN2803.In_7, 74HC595.Q1
  N13: ULN2803.In_8, 74HC595.Q0
  N14: ULN2803.COM_-_Common, 1K-Pullup_-->.pin1, Q8.source, Q7.source, Q6.source, Q5.source, Q4.source, Q3.source, Q2.source, Q1.source, J10.pin2, D1.A, C2.+
  N15: ULN2803.Out_8, 1K-Pullup_-->.pin2, Q1.gate
  N16: ULN2803.Out_7, 1K-Pullup_-->.pin3, Q2.gate
  N17: ULN2803.Out_6, 1K-Pullup_-->.pin4, Q3.gate
  N18: ULN2803.Out_5, 1K-Pullup_-->.pin5, Q4.gate
  N19: ULN2803.Out_4, 1K-Pullup_-->.pin6, Q5.gate
  N20: ULN2803.Out_3, 1K-Pullup_-->.pin7, Q6.gate
  N21: ULN2803.Out_2, 1K-Pullup_-->.pin8, Q7.gate
  N22: ULN2803.Out_1, 1K-Pullup_-->.pin9, Q8.gate
  N23: Q8.drain, J6.pin2
  N24: Q7.drain, J6.pin1
  N25: Q6.drain, J7.pin2
  N26: Q5.drain, J7.pin1
  N27: Q4.drain, J8.pin2
  N28: Q3.drain, J8.pin1
  N29: Q2.drain, J9.pin2
  N30: Q1.drain, J9.pin1
  N31: 74HC595.Q7', IN-BLUE.pin4
  N32: 74HC245.A1, OUT-GREEN.pin4
  N33: 74HC245.A2, OUT-GREEN.pin3
  N34: 74HC245.A3, OUT-GREEN.pin2
  N35: 74HC245.A4, OUT-GREEN.pin1
  N36: 74HC245.A5, OUT-BLUE.pin4
  N37: 74HC245.A6, OUT-BLUE.pin3
  N38: 74HC245.A7, OUT-BLUE.pin2
  N39: 74HC245.A8, OUT-BLUE.pin1
  N40: 74HC245.B8, IN-GREEN.pin1
  N41: 74HC245.B7, IN-GREEN.pin2
  N42: 74HC245.B6, IN-GREEN.pin3
  N43: 74HC245.B5, IN-GREEN.pin4
  N44: 74HC245.B4, IN-RED.pin1
  N45: 74HC245.B3, IN-RED.pin2
  N46: 74HC245.B2, IN-RED.pin3
  N47: 74HC245.B1, IN-RED.pin4

notes:
  USB
  C
  PA7 -MOSI
  PA0 - OE/
  PA1 - LE
  PA5 -CLK
  5V - IN
  5V
  GND
  3.3V - OUT
  Q1-Q8 : IRF9530

custom parts:
  74LVC245 Octal 2-Way Tranceiver: 74LVC245 Octal Bi-directional Tri-state Transceiver
